// Logisim project 8BItComputer_v2.0.circ as structural Verilog: 8 circuits, main circuit main
module main (
  input  in_1,
  input  in_2,
  input  in_3,
  input  in_4,
  input  in_5,
  input  [3:0] in_6,
  input  in_7,
  input  [3:0] in_8,
  input  in_9,
  input  in_10,
  input  in_11,
  input  in_12,
  input  in_13,
  input  in_14,
  input  [7:0] in_15,
  input  in_16,
  input  [7:0] in_17,
  input  in_18,
  input  in_19,
  input  in_20,
  input  in_21,
  input  in_22,
  input  in_23,
  input  in_24,
  input  in_25,
  input  in_26,
  input  in_27,
  input  in_28,
  output [3:0] PC_Content,
  output [3:0] out_30,
  output [3:0] out_31,
  output [7:0] out_32,
  output [7:0] out_33,
  output [7:0] out_34,
  output [7:0] out_35,
  output [7:0] out_36,
  output [2:0] out_37,
  output [7:0] out_38
);

  wire CE, CLK, INTERNAL_OE, OE_ALU, OE_IR, OE_MAR, OE_MBR, OE_OR, OE_PC, OE_RAM, WE_IR, WE_MAR, WE_MBR,
       WE_OR, WE_RA, WE_RAM, WE_RB;
  wire [3:0] bitselector_2_out, decimaldecoder_6_dout_2, EXT_ADDR_BUS, INT_ADDR_BUS;
  wire [7:0] bit_extender_1_out, bit_extender_2_out, bit_extender_3_out, bit_extender_4_out,
       bit_extender_5_out, EXT_DATA_BUS, Instruction_Register_dout;
  wire [31:0] decimaldecoder_1_dout, decimaldecoder_2_dout, decimaldecoder_3_dout, decimaldecoder_4_dout,
       decimaldecoder_5_dout, decimaldecoder_6_dout, decimaldecoder_7_dout, decimaldecoder_8_dout,
       decimaldecoder_9_dout, decimaldecoder_10_dout, decimaldecoder_11_dout, decimaldecoder_12_dout,
       decimaldecoder_13_dout;

  Counter #(.width(4), .max('h6)) Program_Counter (
    .D(INT_ADDR_BUS), .count(CE), .Q(out_30), .clk(CLK));  // open: load, carry, clr
  assign INT_ADDR_BUS = OE_PC ? out_30 : 4'bz;  // Controlled_Buffer controlled_buffer_1
  assign bit_extender_1_out = {{4{1'b0}}, out_30};  // Bit_Extender bit_extender_1
  BitSelector #(.group(4)) bitselector_1 (.in(Instruction_Register_dout), .out(INT_ADDR_BUS), .sel(1'b0));
  Register Instruction_Register (
    .OE(OE_IR), .Din(EXT_DATA_BUS), .WE(WE_IR), .Clock(CLK), .Dout(Instruction_Register_dout),
    .StoredData(out_33));  // open: Reset
  Register Register_A (
    .OE(in_21), .Din(EXT_DATA_BUS), .WE(WE_RA), .Clock(CLK), .Dout(EXT_DATA_BUS), .StoredData(out_34));  // open: Reset
  ALU alu_1 (.Reg_A(out_34), .Reg_B(out_38), .OE(OE_ALU), .Dout(EXT_DATA_BUS), .ALU_Result(out_36));  // open: Carry_Out
  Register Register_B (
    .OE(in_26), .Din(EXT_DATA_BUS), .WE(WE_RB), .Clock(CLK), .Dout(EXT_DATA_BUS), .StoredData(out_38));  // open: Reset
  DecimalDecoder decimaldecoder_1 (.Din(bit_extender_1_out), .Dout(decimaldecoder_1_dout));
  _7_Segment_Display u_7_segment_display_1 (
    .g(decimaldecoder_2_dout[15]), .f(decimaldecoder_2_dout[14]), .a(decimaldecoder_2_dout[13]),
    .b(decimaldecoder_2_dout[12]), .e(decimaldecoder_2_dout[31]), .d(decimaldecoder_2_dout[30]),
    .c(decimaldecoder_2_dout[29]), .dp(decimaldecoder_2_dout[28]));
  DecimalDecoder decimaldecoder_2 (.Din(out_33), .Dout(decimaldecoder_2_dout));
  _7_Segment_Display u_7_segment_display_2 (
    .g(decimaldecoder_3_dout[15]), .f(decimaldecoder_3_dout[14]), .a(decimaldecoder_3_dout[13]),
    .b(decimaldecoder_3_dout[12]), .e(decimaldecoder_3_dout[31]), .d(decimaldecoder_3_dout[30]),
    .c(decimaldecoder_3_dout[29]), .dp(decimaldecoder_3_dout[28]));
  DecimalDecoder decimaldecoder_3 (.Din(out_34), .Dout(decimaldecoder_3_dout));
  _7_Segment_Display u_7_segment_display_3 (
    .g(decimaldecoder_4_dout[15]), .f(decimaldecoder_4_dout[14]), .a(decimaldecoder_4_dout[13]),
    .b(decimaldecoder_4_dout[12]), .e(decimaldecoder_4_dout[31]), .d(decimaldecoder_4_dout[30]),
    .c(decimaldecoder_4_dout[29]), .dp(decimaldecoder_4_dout[28]));
  DecimalDecoder decimaldecoder_4 (.Din(out_36), .Dout(decimaldecoder_4_dout));
  _7_Segment_Display u_7_segment_display_4 (
    .g(decimaldecoder_5_dout[15]), .f(decimaldecoder_5_dout[14]), .a(decimaldecoder_5_dout[13]),
    .b(decimaldecoder_5_dout[12]), .e(decimaldecoder_5_dout[31]), .d(decimaldecoder_5_dout[30]),
    .c(decimaldecoder_5_dout[29]), .dp(decimaldecoder_5_dout[28]));
  DecimalDecoder decimaldecoder_5 (.Din(out_38), .Dout(decimaldecoder_5_dout));
  _7_Segment_Display u_7_segment_display_5 (
    .g(decimaldecoder_1_dout[3]), .f(decimaldecoder_1_dout[2]), .a(decimaldecoder_1_dout[1]),
    .b(decimaldecoder_1_dout[0]), .e(decimaldecoder_1_dout[19]), .d(decimaldecoder_1_dout[18]),
    .c(decimaldecoder_1_dout[17]), .dp(decimaldecoder_1_dout[16]));
  _7_Segment_Display u_7_segment_display_6 (
    .g(decimaldecoder_2_dout[7]), .f(decimaldecoder_2_dout[6]), .a(decimaldecoder_2_dout[5]),
    .b(decimaldecoder_2_dout[4]), .e(decimaldecoder_2_dout[23]), .d(decimaldecoder_2_dout[22]),
    .c(decimaldecoder_2_dout[21]), .dp(decimaldecoder_2_dout[20]));
  _7_Segment_Display u_7_segment_display_7 (
    .g(decimaldecoder_2_dout[11]), .f(decimaldecoder_2_dout[10]), .a(decimaldecoder_2_dout[9]),
    .b(decimaldecoder_2_dout[8]), .e(decimaldecoder_2_dout[27]), .d(decimaldecoder_2_dout[26]),
    .c(decimaldecoder_2_dout[25]), .dp(decimaldecoder_2_dout[24]));
  _7_Segment_Display u_7_segment_display_8 (
    .g(decimaldecoder_3_dout[7]), .f(decimaldecoder_3_dout[6]), .a(decimaldecoder_3_dout[5]),
    .b(decimaldecoder_3_dout[4]), .e(decimaldecoder_3_dout[23]), .d(decimaldecoder_3_dout[22]),
    .c(decimaldecoder_3_dout[21]), .dp(decimaldecoder_3_dout[20]));
  _7_Segment_Display u_7_segment_display_9 (
    .g(decimaldecoder_3_dout[11]), .f(decimaldecoder_3_dout[10]), .a(decimaldecoder_3_dout[9]),
    .b(decimaldecoder_3_dout[8]), .e(decimaldecoder_3_dout[27]), .d(decimaldecoder_3_dout[26]),
    .c(decimaldecoder_3_dout[25]), .dp(decimaldecoder_3_dout[24]));
  _7_Segment_Display u_7_segment_display_10 (
    .g(decimaldecoder_4_dout[11]), .f(decimaldecoder_4_dout[10]), .a(decimaldecoder_4_dout[9]),
    .b(decimaldecoder_4_dout[8]), .e(decimaldecoder_4_dout[27]), .d(decimaldecoder_4_dout[26]),
    .c(decimaldecoder_4_dout[25]), .dp(decimaldecoder_4_dout[24]));
  _7_Segment_Display u_7_segment_display_11 (
    .g(decimaldecoder_4_dout[7]), .f(decimaldecoder_4_dout[6]), .a(decimaldecoder_4_dout[5]),
    .b(decimaldecoder_4_dout[4]), .e(decimaldecoder_4_dout[23]), .d(decimaldecoder_4_dout[22]),
    .c(decimaldecoder_4_dout[21]), .dp(decimaldecoder_4_dout[20]));
  _7_Segment_Display u_7_segment_display_12 (
    .g(decimaldecoder_5_dout[11]), .f(decimaldecoder_5_dout[10]), .a(decimaldecoder_5_dout[9]),
    .b(decimaldecoder_5_dout[8]), .e(decimaldecoder_5_dout[27]), .d(decimaldecoder_5_dout[26]),
    .c(decimaldecoder_5_dout[25]), .dp(decimaldecoder_5_dout[24]));
  _7_Segment_Display u_7_segment_display_13 (
    .g(decimaldecoder_5_dout[7]), .f(decimaldecoder_5_dout[6]), .a(decimaldecoder_5_dout[5]),
    .b(decimaldecoder_5_dout[4]), .e(decimaldecoder_5_dout[23]), .d(decimaldecoder_5_dout[22]),
    .c(decimaldecoder_5_dout[21]), .dp(decimaldecoder_5_dout[20]));
  _7_Segment_Display u_7_segment_display_14 (
    .g(decimaldecoder_2_dout[3]), .f(decimaldecoder_2_dout[2]), .a(decimaldecoder_2_dout[1]),
    .b(decimaldecoder_2_dout[0]), .e(decimaldecoder_2_dout[19]), .d(decimaldecoder_2_dout[18]),
    .c(decimaldecoder_2_dout[17]), .dp(decimaldecoder_2_dout[16]));
  _7_Segment_Display u_7_segment_display_15 (
    .g(decimaldecoder_3_dout[3]), .f(decimaldecoder_3_dout[2]), .a(decimaldecoder_3_dout[1]),
    .b(decimaldecoder_3_dout[0]), .e(decimaldecoder_3_dout[19]), .d(decimaldecoder_3_dout[18]),
    .c(decimaldecoder_3_dout[17]), .dp(decimaldecoder_3_dout[16]));
  _7_Segment_Display u_7_segment_display_16 (
    .g(decimaldecoder_4_dout[3]), .f(decimaldecoder_4_dout[2]), .a(decimaldecoder_4_dout[1]),
    .b(decimaldecoder_4_dout[0]), .e(decimaldecoder_4_dout[19]), .d(decimaldecoder_4_dout[18]),
    .c(decimaldecoder_4_dout[17]), .dp(decimaldecoder_4_dout[16]));
  _7_Segment_Display u_7_segment_display_17 (
    .g(decimaldecoder_5_dout[3]), .f(decimaldecoder_5_dout[2]), .a(decimaldecoder_5_dout[1]),
    .b(decimaldecoder_5_dout[0]), .e(decimaldecoder_5_dout[19]), .d(decimaldecoder_5_dout[18]),
    .c(decimaldecoder_5_dout[17]), .dp(decimaldecoder_5_dout[16]));
  Controlled_Buffer #(.width(4)) controlled_buffer_2 (.in(in_6), .en(in_3));  // open: out
  Controlled_Buffer #(.width(8)) controlled_buffer_3 (.in(in_17), .en(in_16));  // open: out
  BitSelector #(.group(4)) bitselector_2 (.in(out_33), .out(bitselector_2_out), .sel(1'b1));
  LED led_1 (.in(INT_ADDR_BUS[2]));
  LED led_2 (.in(INT_ADDR_BUS[3]));
  assign bit_extender_2_out = {{4{1'b0}}, INT_ADDR_BUS};  // Bit_Extender bit_extender_2
  Clock clock_1 (.out(CLK));
  LED led_3 (.in(EXT_DATA_BUS[6]));
  LED led_4 (.in(EXT_DATA_BUS[7]));
  _7_Segment_Display u_7_segment_display_18 (
    .g(decimaldecoder_6_dout[15]), .f(decimaldecoder_6_dout[14]), .a(decimaldecoder_6_dout[13]),
    .b(decimaldecoder_6_dout[12]), .e(decimaldecoder_6_dout[31]), .d(decimaldecoder_6_dout[30]),
    .c(decimaldecoder_6_dout[29]), .dp(decimaldecoder_6_dout[28]));
  DecimalDecoder decimaldecoder_6 (
    .Din(EXT_DATA_BUS),
    .Dout({decimaldecoder_6_dout[31:20], decimaldecoder_6_dout_2, decimaldecoder_6_dout[15:0]}));
  LED led_5 (.in(INT_ADDR_BUS[1]));
  LED led_6 (.in(INT_ADDR_BUS[0]));
  DecimalDecoder decimaldecoder_7 (.Din(bit_extender_2_out), .Dout(decimaldecoder_7_dout));
  LED led_7 (.in(EXT_DATA_BUS[3]));
  LED led_8 (.in(EXT_DATA_BUS[5]));
  LED led_9 (.in(EXT_DATA_BUS[4]));
  _7_Segment_Display u_7_segment_display_19 (
    .g(decimaldecoder_6_dout[7]), .f(decimaldecoder_6_dout[6]), .a(decimaldecoder_6_dout[5]),
    .b(decimaldecoder_6_dout[4]), .e(decimaldecoder_6_dout[23]), .d(decimaldecoder_6_dout[22]),
    .c(decimaldecoder_6_dout[21]), .dp(decimaldecoder_6_dout[20]));
  _7_Segment_Display u_7_segment_display_20 (
    .g(decimaldecoder_6_dout[11]), .f(decimaldecoder_6_dout[10]), .a(decimaldecoder_6_dout[9]),
    .b(decimaldecoder_6_dout[8]), .e(decimaldecoder_6_dout[27]), .d(decimaldecoder_6_dout[26]),
    .c(decimaldecoder_6_dout[25]), .dp(decimaldecoder_6_dout[24]));
  CU_I cu_i_1 (
    .OPC3(bitselector_2_out[3]), .C0(OE_PC), .OPC2(bitselector_2_out[2]), .OPC1(bitselector_2_out[1]),
    .C1(CE), .OPC0(bitselector_2_out[0]), .C2(WE_RAM), .SC2(out_37[2]), .SC1(out_37[1]), .SC0(out_37[0]),
    .C3(OE_RAM), .C4(WE_MBR), .C5(INTERNAL_OE), .C6(OE_MBR), .C7(WE_IR), .C8(OE_IR), .C9(WE_MAR),
    .C10(OE_MAR), .C11(OE_ALU));
  CU_II cu_ii_1 (
    .OPC3(bitselector_2_out[3]), .OPC2(bitselector_2_out[2]), .OPC1(bitselector_2_out[1]), .C12(WE_RA),
    .OPC0(bitselector_2_out[0]), .SC2(out_37[2]), .C13(WE_RB), .SC1(out_37[1]), .SC0(out_37[0]), .C14(OE_OR),
    .C15(WE_OR), .C16(in_21), .C17(in_26));
  _7_Segment_Display u_7_segment_display_21 (
    .g(decimaldecoder_7_dout[3]), .f(decimaldecoder_7_dout[2]), .a(decimaldecoder_7_dout[1]),
    .b(decimaldecoder_7_dout[0]), .e(decimaldecoder_7_dout[19]), .d(decimaldecoder_7_dout[18]),
    .c(decimaldecoder_7_dout[17]), .dp(decimaldecoder_7_dout[16]));
  LED led_10 (.in(EXT_DATA_BUS[1]));
  LED led_11 (.in(EXT_DATA_BUS[2]));
  LED led_12 (.in(EXT_DATA_BUS[0]));
  _7_Segment_Display u_7_segment_display_22 (
    .g(decimaldecoder_6_dout[3]), .f(decimaldecoder_6_dout[2]), .a(decimaldecoder_6_dout[1]),
    .b(decimaldecoder_6_dout[0]), .e(decimaldecoder_6_dout_2[3]), .d(decimaldecoder_6_dout_2[2]),
    .c(decimaldecoder_6_dout_2[1]), .dp(decimaldecoder_6_dout_2[0]));
  MAR MAR (.Din(INT_ADDR_BUS), .WE(WE_MAR), .OE(OE_MAR), .Clk(CLK), .Dout(EXT_ADDR_BUS), .SD(out_31));  // open: Reset
  Register MBR (
    .OE(OE_MBR), .Din(EXT_DATA_BUS), .WE(WE_MBR), .Clock(CLK), .Dout(EXT_DATA_BUS), .StoredData(out_32));  // open: Reset
  assign EXT_DATA_BUS = INTERNAL_OE ? out_32 : 8'bz;  // Controlled_Buffer controlled_buffer_4
  Register Output_Register (
    .OE(OE_OR), .Din(EXT_DATA_BUS), .WE(WE_OR), .Clock(CLK), .Dout(EXT_DATA_BUS), .StoredData(out_35));  // open: Reset
  assign bit_extender_3_out = {{4{1'b0}}, out_31};  // Bit_Extender bit_extender_3
  DecimalDecoder decimaldecoder_8 (.Din(out_32), .Dout(decimaldecoder_8_dout));
  DecimalDecoder decimaldecoder_9 (.Din(out_35), .Dout(decimaldecoder_9_dout));
  DecimalDecoder decimaldecoder_10 (.Din(bit_extender_3_out), .Dout(decimaldecoder_10_dout));
  _7_Segment_Display u_7_segment_display_23 (
    .g(decimaldecoder_8_dout[15]), .f(decimaldecoder_8_dout[14]), .a(decimaldecoder_8_dout[13]),
    .b(decimaldecoder_8_dout[12]), .e(decimaldecoder_8_dout[31]), .d(decimaldecoder_8_dout[30]),
    .c(decimaldecoder_8_dout[29]), .dp(decimaldecoder_8_dout[28]));
  _7_Segment_Display u_7_segment_display_24 (
    .g(decimaldecoder_9_dout[15]), .f(decimaldecoder_9_dout[14]), .a(decimaldecoder_9_dout[13]),
    .b(decimaldecoder_9_dout[12]), .e(decimaldecoder_9_dout[31]), .d(decimaldecoder_9_dout[30]),
    .c(decimaldecoder_9_dout[29]), .dp(decimaldecoder_9_dout[28]));
  _7_Segment_Display u_7_segment_display_25 (
    .g(decimaldecoder_10_dout[3]), .f(decimaldecoder_10_dout[2]), .a(decimaldecoder_10_dout[1]),
    .b(decimaldecoder_10_dout[0]), .e(decimaldecoder_10_dout[19]), .d(decimaldecoder_10_dout[18]),
    .c(decimaldecoder_10_dout[17]), .dp(decimaldecoder_10_dout[16]));
  _7_Segment_Display u_7_segment_display_26 (
    .g(decimaldecoder_8_dout[7]), .f(decimaldecoder_8_dout[6]), .a(decimaldecoder_8_dout[5]),
    .b(decimaldecoder_8_dout[4]), .e(decimaldecoder_8_dout[23]), .d(decimaldecoder_8_dout[22]),
    .c(decimaldecoder_8_dout[21]), .dp(decimaldecoder_8_dout[20]));
  _7_Segment_Display u_7_segment_display_27 (
    .g(decimaldecoder_8_dout[11]), .f(decimaldecoder_8_dout[10]), .a(decimaldecoder_8_dout[9]),
    .b(decimaldecoder_8_dout[8]), .e(decimaldecoder_8_dout[27]), .d(decimaldecoder_8_dout[26]),
    .c(decimaldecoder_8_dout[25]), .dp(decimaldecoder_8_dout[24]));
  _7_Segment_Display u_7_segment_display_28 (
    .g(decimaldecoder_9_dout[7]), .f(decimaldecoder_9_dout[6]), .a(decimaldecoder_9_dout[5]),
    .b(decimaldecoder_9_dout[4]), .e(decimaldecoder_9_dout[23]), .d(decimaldecoder_9_dout[22]),
    .c(decimaldecoder_9_dout[21]), .dp(decimaldecoder_9_dout[20]));
  _7_Segment_Display u_7_segment_display_29 (
    .g(decimaldecoder_9_dout[11]), .f(decimaldecoder_9_dout[10]), .a(decimaldecoder_9_dout[9]),
    .b(decimaldecoder_9_dout[8]), .e(decimaldecoder_9_dout[27]), .d(decimaldecoder_9_dout[26]),
    .c(decimaldecoder_9_dout[25]), .dp(decimaldecoder_9_dout[24]));
  RAM #(.addrWidth(4), .bus("separate")) ram_1 (
    .addr(EXT_ADDR_BUS), .din(EXT_DATA_BUS), .data(EXT_DATA_BUS), .str(WE_RAM), .clk(CLK), .ld(OE_RAM));  // open: sel, clr
  _7_Segment_Display u_7_segment_display_30 (
    .g(decimaldecoder_8_dout[3]), .f(decimaldecoder_8_dout[2]), .a(decimaldecoder_8_dout[1]),
    .b(decimaldecoder_8_dout[0]), .e(decimaldecoder_8_dout[19]), .d(decimaldecoder_8_dout[18]),
    .c(decimaldecoder_8_dout[17]), .dp(decimaldecoder_8_dout[16]));
  _7_Segment_Display u_7_segment_display_31 (
    .g(decimaldecoder_9_dout[3]), .f(decimaldecoder_9_dout[2]), .a(decimaldecoder_9_dout[1]),
    .b(decimaldecoder_9_dout[0]), .e(decimaldecoder_9_dout[19]), .d(decimaldecoder_9_dout[18]),
    .c(decimaldecoder_9_dout[17]), .dp(decimaldecoder_9_dout[16]));
  Counter #(.width(3), .max('h5)) Step_Counter (.Q(out_37), .clk(CLK));  // open: load, D, count, carry, clr
  Controlled_Buffer #(.width(4)) controlled_buffer_5 (.in(in_8), .en(in_7));  // open: out
  Controlled_Buffer #(.width(8)) controlled_buffer_6 (.in(in_15), .en(in_13));  // open: out
  _7_Segment_Display u_7_segment_display_32 (
    .g(decimaldecoder_11_dout[15]), .f(decimaldecoder_11_dout[14]), .a(decimaldecoder_11_dout[13]),
    .b(decimaldecoder_11_dout[12]), .e(decimaldecoder_11_dout[31]), .d(decimaldecoder_11_dout[30]),
    .c(decimaldecoder_11_dout[29]), .dp(decimaldecoder_11_dout[28]));
  DecimalDecoder decimaldecoder_11 (.Din(EXT_DATA_BUS), .Dout(decimaldecoder_11_dout));
  assign bit_extender_4_out = {{5{1'b0}}, out_37};  // Bit_Extender bit_extender_4
  LED led_13 (.in(EXT_ADDR_BUS[3]));
  LED led_14 (.in(EXT_ADDR_BUS[1]));
  LED led_15 (.in(EXT_ADDR_BUS[2]));
  assign bit_extender_5_out = {{4{1'b0}}, EXT_ADDR_BUS};  // Bit_Extender bit_extender_5
  LED led_16 (.in(EXT_DATA_BUS[4]));
  LED led_17 (.in(EXT_DATA_BUS[5]));
  LED led_18 (.in(EXT_DATA_BUS[7]));
  LED led_19 (.in(EXT_DATA_BUS[6]));
  _7_Segment_Display u_7_segment_display_33 (
    .g(decimaldecoder_11_dout[11]), .f(decimaldecoder_11_dout[10]), .a(decimaldecoder_11_dout[9]),
    .b(decimaldecoder_11_dout[8]), .e(decimaldecoder_11_dout[27]), .d(decimaldecoder_11_dout[26]),
    .c(decimaldecoder_11_dout[25]), .dp(decimaldecoder_11_dout[24]));
  _7_Segment_Display u_7_segment_display_34 (
    .g(decimaldecoder_11_dout[7]), .f(decimaldecoder_11_dout[6]), .a(decimaldecoder_11_dout[5]),
    .b(decimaldecoder_11_dout[4]), .e(decimaldecoder_11_dout[23]), .d(decimaldecoder_11_dout[22]),
    .c(decimaldecoder_11_dout[21]), .dp(decimaldecoder_11_dout[20]));
  DecimalDecoder decimaldecoder_12 (.Din(bit_extender_4_out), .Dout(decimaldecoder_12_dout));
  LED led_20 (.in(EXT_ADDR_BUS[0]));
  _7_Segment_Display u_7_segment_display_35 (
    .g(decimaldecoder_13_dout[3]), .f(decimaldecoder_13_dout[2]), .a(decimaldecoder_13_dout[1]),
    .b(decimaldecoder_13_dout[0]), .e(decimaldecoder_13_dout[19]), .d(decimaldecoder_13_dout[18]),
    .c(decimaldecoder_13_dout[17]), .dp(decimaldecoder_13_dout[16]));
  DecimalDecoder decimaldecoder_13 (.Din(bit_extender_5_out), .Dout(decimaldecoder_13_dout));
  LED led_21 (.in(EXT_DATA_BUS[3]));
  LED led_22 (.in(EXT_DATA_BUS[2]));
  LED led_23 (.in(EXT_DATA_BUS[0]));
  LED led_24 (.in(EXT_DATA_BUS[1]));
  _7_Segment_Display u_7_segment_display_36 (
    .g(decimaldecoder_11_dout[3]), .f(decimaldecoder_11_dout[2]), .a(decimaldecoder_11_dout[1]),
    .b(decimaldecoder_11_dout[0]), .e(decimaldecoder_11_dout[19]), .d(decimaldecoder_11_dout[18]),
    .c(decimaldecoder_11_dout[17]), .dp(decimaldecoder_11_dout[16]));
  _7_Segment_Display u_7_segment_display_37 (
    .g(decimaldecoder_12_dout[3]), .f(decimaldecoder_12_dout[2]), .a(decimaldecoder_12_dout[1]),
    .b(decimaldecoder_12_dout[0]), .e(decimaldecoder_12_dout[19]), .d(decimaldecoder_12_dout[18]),
    .c(decimaldecoder_12_dout[17]), .dp(decimaldecoder_12_dout[16]));

  assign PC_Content = out_30;

  // Other names for the same wires on the sheet: ALU[7:0] = out_36; INT_DATA_BUS[7:0] = EXT_DATA_BUS;
  //   IR[7:0] = out_33; MAR[3:0] = out_31; MBR[7:0] = out_32; OE_RA = in_21; OE_RB = in_26; OE_SC = in_28;
  //   OR[7:0] = out_35; PC[3:0] = out_30; RA[7:0] = out_34; RB[7:0] = out_38; SC[2:0] = out_37; SCE = in_27

  // Notes on the sheet:
  //   Program Counter
  //   Register A
  //   ALU
  //   Register B
  //   Instruction Register
  //   Internal Address Bus
  //   Internal Data Bus
  //   MAR
  //   MBR
  //   Output Register
  //   External Address Bus
  //   External Data Bus
  //   Step Counter
endmodule

module MemoryCell (
  input  Clock,
  input  WE,
  input  Din,
  input  OE,
  input  Reset,
  output Dout,
  output StoredData
);

  wire and_1_out, and_2_out, not_1_out, or_1_out;

  not not_1 (not_1_out, WE);
  and and_1 (and_1_out, StoredData, not_1_out);
  and and_2 (and_2_out, WE, Din);
  or or_1 (or_1_out, and_1_out, and_2_out);
  D_Flip_Flop d_ff_1 (.clk(Clock), .D(or_1_out), .Q(StoredData), .reset(Reset));  // open: Qn, preset, en
  assign Dout = OE ? StoredData : 1'bz;  // Controlled_Buffer controlled_buffer_1
endmodule

module Register (
  input  Reset,
  input  OE,
  input  [7:0] Din,
  input  WE,
  input  Clock,
  output [7:0] Dout,
  output [7:0] StoredData
);

  MemoryCell R0 (
    .Clock(Clock), .WE(WE), .Din(Din[0]), .OE(OE), .Reset(Reset), .Dout(Dout[0]), .StoredData(StoredData[0]));
  MemoryCell R1 (
    .Clock(Clock), .WE(WE), .Din(Din[1]), .OE(OE), .Reset(Reset), .Dout(Dout[1]), .StoredData(StoredData[1]));
  MemoryCell R2 (
    .Clock(Clock), .WE(WE), .Din(Din[2]), .OE(OE), .Dout(Dout[2]), .StoredData(StoredData[2]));  // open: Reset
  MemoryCell R (
    .Clock(Clock), .WE(WE), .Din(Din[3]), .OE(OE), .Reset(Reset), .Dout(Dout[3]), .StoredData(StoredData[3]));
  MemoryCell R_2 (
    .Clock(Clock), .WE(WE), .Din(Din[4]), .OE(OE), .Reset(Reset), .Dout(Dout[4]), .StoredData(StoredData[4]));
  MemoryCell R5 (
    .Clock(Clock), .WE(WE), .Din(Din[5]), .OE(OE), .Reset(Reset), .Dout(Dout[5]), .StoredData(StoredData[5]));
  MemoryCell R6 (
    .Clock(Clock), .WE(WE), .Din(Din[6]), .OE(OE), .Reset(Reset), .Dout(Dout[6]), .StoredData(StoredData[6]));
  MemoryCell R7 (
    .Clock(Clock), .WE(WE), .Din(Din[7]), .OE(OE), .Reset(Reset), .Dout(Dout[7]), .StoredData(StoredData[7]));
endmodule

module MAR (
  input  [3:0] Din,
  input  WE,
  input  OE,
  input  Clk,
  input  Reset,
  output [3:0] Dout,
  output [3:0] SD
);

  MemoryCell memorycell_1 (
    .Clock(Clk), .WE(WE), .Din(Din[0]), .OE(OE), .Reset(Reset), .Dout(Dout[0]), .StoredData(SD[0]));
  MemoryCell memorycell_2 (
    .Clock(Clk), .WE(WE), .Din(Din[1]), .OE(OE), .Reset(Reset), .Dout(Dout[1]), .StoredData(SD[1]));
  MemoryCell memorycell_3 (
    .Clock(Clk), .WE(WE), .Din(Din[2]), .OE(OE), .Reset(Reset), .Dout(Dout[2]), .StoredData(SD[2]));
  MemoryCell memorycell_4 (
    .Clock(Clk), .WE(WE), .Din(Din[3]), .OE(OE), .Reset(Reset), .Dout(Dout[3]), .StoredData(SD[3]));

  // Notes on the sheet:
  //   Memory Address Register
endmodule

module ALU (
  input  [7:0] Reg_A,
  input  [7:0] Reg_B,
  input  OE,
  output [7:0] Dout,
  output [7:0] ALU_Result,
  output Carry_Out
);

  Adder adder_1 (.a(Reg_A), .b(Reg_B), .out(ALU_Result), .cout(Carry_Out));  // open: cin
  assign Dout = OE ? ALU_Result : 8'bz;  // Controlled_Buffer controlled_buffer_1

  // Notes on the sheet:
  //   ALU (8Bit)
endmodule

module DecimalDecoder (
  input  [7:0] Din,
  output [31:0] Dout
);

  ROM #(.dataWidth(32)) rom_1 (
    .addr(Din),
    .data({Dout[31:28], Dout[15:12], Dout[27:24], Dout[11:8], Dout[23:20], Dout[7:4], Dout[19:16], Dout[3:0]}));  // open: sel

  // Notes on the sheet:
  //   contents of rom_1 (hex, n*v repeats v):
  //   e7 21 cb 6b 2d 6e ee 23 ef 2f 21e7 2121 21cb 216b 212d 216e 21ee 2123 21ef 212f cbe7 cb21 cbcb cb6b
  //   cb2d cb6e cbee cb23 cbef cb2f 6be7 6b21 6bcb 6b6b 6b2d 6b6e 6bee 6b23 6bef 6b2f 2de7 2d21 2dcb 2d6b
  //   2d2d 2d6e 2dee 2d23 2def 2d2f 6ee7 6e21 6ecb 6e6b 6e2d 6e6e 6eee 6e23 6eef 6e2f eee7 ee21 eecb ee6b
  //   ee2d ee6e eeee ee23 eeef ee2f 23e7 2321 23cb 236b 232d 236e 23ee 2323 23ef 232f efe7 ef21 efcb ef6b
  //   ef2d ef6e efee ef23 efef ef2f 2fe7 2f21 2fcb 2f6b 2f2d 2f6e 2fee 2f23 2fef 2f2f 21e7e7 21e721 21e7cb
  //   21e76b 21e72d 21e76e 21e7ee 21e723 21e7ef 21e72f 2121e7 212121 2121cb 21216b 21212d 21216e 2121ee
  //   212123 2121ef 21212f 21cbe7 21cb21 21cbcb 21cb6b 21cb2d 21cb6e 21cbee 21cb23 21cbef 21cb2f 216be7
  //   216b21 216bcb 216b6b 216b2d 216b6e 216bee 216b23 216bef 216b2f 212de7 212d21 212dcb 212d6b 212d2d
  //   212d6e 212dee 212d23 212def 212d2f 216ee7 216e21 216ecb 216e6b 216e2d 216e6e 216eee 216e23 216eef
  //   216e2f 21eee7 21ee21 21eecb 21ee6b 21ee2d 21ee6e 21eeee 21ee23 21eeef 21ee2f 2123e7 212321 2123cb
  //   21236b 21232d 21236e 2123ee 212323 2123ef 21232f 21efe7 21ef21 21efcb 21ef6b 21ef2d 21ef6e 21efee
  //   21ef23 21efef 21ef2f 212fe7 212f21 212fcb 212f6b 212f2d 212f6e 212fee 212f23 212fef 212f2f cbe7e7
  //   cbe721 cbe7cb cbe76b cbe72d cbe76e cbe7ee cbe723 cbe7ef cbe72f cb21e7 cb2121 cb21cb cb216b cb212d
  //   cb216e cb21ee cb2123 cb21ef cb212f cbcbe7 cbcb21 cbcbcb cbcb6b cbcb2d cbcb6e cbcbee cbcb23 cbcbef
  //   cbcb2f cb6be7 cb6b21 cb6bcb cb6b6b cb6b2d cb6b6e cb6bee cb6b23 cb6bef cb6b2f cb2de7 cb2d21 cb2dcb
  //   cb2d6b cb2d2d cb2d6e cb2dee cb2d23 cb2def cb2d2f cb6ee7 cb6e21 cb6ecb cb6e6b cb6e2d cb6e6e
endmodule

module CU_II (
  input  OPC3,
  input  OPC2,
  input  OPC1,
  input  OPC0,
  input  SC2,
  input  SC1,
  input  SC0,
  output C12,
  output C13,
  output C14,
  output C15,
  output C16,
  output C17
);

  wire and_1_out, and_2_out, not_1_out, not_2_out, not_3_out, not_4_out, not_5_out, not_6_out, not_7_out,
       not_8_out, not_9_out, not_10_out, not_11_out, not_12_out, not_13_out, not_14_out;

  not not_1 (not_1_out, OPC2);
  not not_2 (not_2_out, OPC1);
  not not_3 (not_3_out, OPC0);
  not not_4 (not_4_out, SC1);
  not not_5 (not_5_out, SC1);
  not not_6 (not_6_out, SC0);
  not not_7 (not_7_out, OPC1);
  not not_8 (not_8_out, SC1);
  not not_9 (not_9_out, SC1);
  not not_10 (not_10_out, SC0);
  not not_11 (not_11_out, SC2);
  not not_12 (not_12_out, OPC0);
  not not_13 (not_13_out, SC2);
  not not_14 (not_14_out, SC2);
  and and_1 (and_1_out, not_1_out, not_2_out, not_3_out, SC2, not_4_out, SC0);
  and and_2 (and_2_out, OPC2, SC2, not_5_out, not_6_out);
  and and_3 (C13, not_7_out, OPC0, SC2, not_8_out, SC0);
  and and_4 (C14, OPC2, SC2, not_9_out, not_10_out);
  and and_5 (C15, OPC2, not_11_out, SC1, SC0);
  and and_6 (C16, OPC1, not_12_out, not_13_out, SC1, SC0);
  and and_7 (C17, OPC1, OPC0, not_14_out, SC1, SC0);
  or or_1 (C12, and_1_out, and_2_out);
endmodule

module CU_I (
  input  OPC3,
  input  OPC2,
  input  OPC1,
  input  OPC0,
  input  SC2,
  input  SC1,
  input  SC0,
  output C0,
  output C1,
  output C2,
  output C3,
  output C4,
  output C5,
  output C6,
  output C7,
  output C8,
  output C9,
  output C10,
  output C11
);

  wire and_4_out, and_5_out, and_6_out, and_7_out, and_8_out, and_9_out, and_10_out, and_14_out, and_15_out,
       and_16_out, and_17_out, not_1_out, not_2_out, not_3_out, not_4_out, not_5_out, not_6_out, not_7_out,
       not_8_out, not_9_out, not_10_out, not_11_out, not_12_out, not_13_out, not_14_out, not_15_out,
       not_16_out, not_17_out, not_18_out, not_19_out, not_20_out, not_21_out, not_22_out, not_23_out,
       not_24_out, not_25_out, not_26_out, not_27_out, not_28_out, not_29_out, not_30_out, not_31_out,
       not_32_out, not_33_out, not_34_out, not_35_out, not_36_out, not_37_out, not_38_out, not_39_out,
       not_40_out, not_41_out, not_42_out;

  not not_1 (not_1_out, SC2);
  not not_2 (not_2_out, SC1);
  not not_3 (not_3_out, SC0);
  not not_4 (not_4_out, SC2);
  not not_5 (not_5_out, SC1);
  not not_6 (not_6_out, SC1);
  not not_7 (not_7_out, SC0);
  not not_8 (not_8_out, SC2);
  not not_9 (not_9_out, SC1);
  not not_10 (not_10_out, OPC2);
  not not_11 (not_11_out, OPC1);
  not not_12 (not_12_out, SC1);
  not not_13 (not_13_out, SC0);
  not not_14 (not_14_out, SC2);
  not not_15 (not_15_out, SC1);
  not not_16 (not_16_out, OPC2);
  not not_17 (not_17_out, OPC1);
  not not_18 (not_18_out, SC1);
  not not_19 (not_19_out, SC0);
  not not_20 (not_20_out, SC2);
  not not_21 (not_21_out, SC2);
  not not_22 (not_22_out, SC0);
  not not_23 (not_23_out, OPC2);
  not not_24 (not_24_out, OPC1);
  not not_25 (not_25_out, SC1);
  not not_26 (not_26_out, SC1);
  not not_27 (not_27_out, SC0);
  not not_28 (not_28_out, SC2);
  not not_29 (not_29_out, SC0);
  not not_30 (not_30_out, OPC2);
  not not_31 (not_31_out, SC2);
  not not_32 (not_32_out, SC2);
  not not_33 (not_33_out, SC1);
  not not_34 (not_34_out, SC0);
  not not_35 (not_35_out, OPC2);
  not not_36 (not_36_out, SC2);
  not not_37 (not_37_out, SC2);
  not not_38 (not_38_out, SC1);
  not not_39 (not_39_out, OPC2);
  not not_40 (not_40_out, SC1);
  not not_41 (not_41_out, SC0);
  not not_42 (not_42_out, SC2);
  and and_1 (C0, not_1_out, not_2_out, not_3_out);
  and and_2 (C1, not_4_out, not_5_out, SC0);
  and and_3 (C2, OPC1, SC2, not_6_out, not_7_out);
  and and_4 (and_4_out, not_8_out, not_9_out, SC0);
  and and_5 (and_5_out, not_10_out, not_11_out, SC2, not_12_out, not_13_out);
  and and_6 (and_6_out, not_14_out, not_15_out, SC0);
  and and_7 (and_7_out, not_16_out, not_17_out, SC2, not_18_out, not_19_out);
  and and_8 (and_8_out, OPC1, not_20_out, SC0);
  and and_9 (and_9_out, not_21_out, SC1, not_22_out);
  and and_10 (and_10_out, not_23_out, not_24_out, SC2, not_25_out, SC0);
  and and_11 (C6, OPC1, SC2, not_26_out, not_27_out);
  and and_12 (C7, not_28_out, SC1, not_29_out);
  and and_13 (C8, not_30_out, not_31_out, SC1, SC0);
  and and_14 (and_14_out, not_32_out, not_33_out, not_34_out);
  and and_15 (and_15_out, not_35_out, not_36_out, SC1, SC0);
  and and_16 (and_16_out, not_37_out, not_38_out, SC0);
  and and_17 (and_17_out, not_39_out, SC2, not_40_out, not_41_out);
  and and_18 (C11, OPC2, not_42_out, SC1, SC0);
  or or_1 (C3, and_4_out, and_5_out);
  or or_2 (C4, and_6_out, and_7_out, and_8_out);
  or or_3 (C5, and_9_out, and_10_out);
  or or_4 (C9, and_14_out, and_15_out);
  or or_5 (C10, and_16_out, and_17_out);
endmodule
