// Logisim project CUNIT.circ as structural Verilog: 1 circuit, main circuit CU
module CU (
  input  opc3,
  input  opc2,
  input  opc1,
  input  opc0,
  input  sc3,
  input  sc2,
  input  sc1,
  input  sc0,
  output OE_PC,
  output CE_PC,
  output WE_RAM,
  output OE_RAM,
  output WE_MBR,
  output IOE_MBR,
  output OR_MBR,
  output WE_IR,
  output OE_IR,
  output WE_MAR,
  output OE_MAR,
  output OE_ALU,
  output WE_RA,
  output OE_RA,
  output WE_RB,
  output OE_RB,
  output WE_OR,
  output OE_OR,
  output WE_ADDR0,
  output OE_ADDR0,
  output WE_ADDR1,
  output OE_ADDR1,
  output WE_VR,
  output OE_VR,
  output DONE_SC,
  output CLK_OFF
);

  wire and_1_out, and_2_out, and_3_out, and_4_out, and_5_out, and_6_out, and_7_out, and_8_out, and_9_out,
       and_10_out, and_11_out, and_12_out, and_14_out, and_15_out, and_16_out, and_17_out, and_18_out,
       and_19_out, and_20_out, and_21_out, and_22_out, and_23_out, and_24_out, and_25_out, and_26_out,
       and_27_out, and_28_out, and_29_out, and_30_out, and_31_out, and_32_out, and_33_out, and_34_out,
       and_35_out, and_38_out, and_39_out, and_40_out, and_41_out, and_42_out, and_43_out, and_44_out,
       and_45_out, and_46_out, and_47_out, and_48_out, and_49_out, and_50_out, and_51_out, and_52_out,
       and_53_out, and_55_out, and_56_out, and_57_out, and_58_out, and_59_out, and_60_out, and_61_out,
       and_62_out, and_63_out, and_64_out, and_65_out, and_68_out, and_69_out, and_70_out, and_71_out,
       and_72_out, and_73_out, and_74_out, and_75_out, and_77_out, and_78_out, and_79_out, and_80_out,
       and_81_out, and_82_out, and_83_out, not_1_out, not_2_out, not_3_out, not_4_out, not_5_out, not_6_out,
       not_7_out, not_8_out;

  not not_1 (not_1_out, opc3);
  not not_2 (not_2_out, opc2);
  not not_3 (not_3_out, opc1);
  not not_4 (not_4_out, opc0);
  not not_5 (not_5_out, sc3);
  not not_6 (not_6_out, sc2);
  not not_7 (not_7_out, sc1);
  not not_8 (not_8_out, sc0);
  and and_1 (and_1_out, not_5_out, not_6_out, not_7_out, not_8_out);
  and and_2 (and_2_out, opc2, not_5_out, not_6_out, sc1, sc0);
  and and_3 (and_3_out, opc3, not_5_out, not_6_out, sc1, sc0);
  and and_4 (and_4_out, opc2, opc1, not_5_out, sc2, sc1, not_8_out);
  and and_5 (and_5_out, opc3, not_5_out, sc2, sc1, not_8_out);
  and and_6 (and_6_out, opc1, opc0, not_5_out, not_6_out, sc1, sc0);
  and and_7 (and_7_out, not_5_out, not_6_out, not_7_out, sc0);
  and and_8 (and_8_out, opc2, not_5_out, sc2, not_7_out, not_8_out);
  and and_9 (and_9_out, opc3, not_5_out, sc2, not_7_out, not_8_out);
  and and_10 (and_10_out, opc2, opc1, not_5_out, sc2, sc1, sc0);
  and and_11 (and_11_out, opc3, not_5_out, sc2, sc1, sc0);
  and and_12 (and_12_out, opc1, opc0, not_5_out, sc2, not_7_out, not_8_out);
  and and_13 (WE_RAM, opc3, sc3, not_6_out, sc1, not_8_out);
  and and_14 (and_14_out, not_5_out, not_6_out, not_7_out, sc0);
  and and_15 (and_15_out, opc2, not_5_out, sc2, not_7_out, not_8_out);
  and and_16 (and_16_out, opc3, not_5_out, sc2, not_7_out, not_8_out);
  and and_17 (and_17_out, opc2, opc1, not_5_out, sc2, sc1, sc0);
  and and_18 (and_18_out, opc3, not_5_out, sc2, sc1, sc0);
  and and_19 (and_19_out, opc2, opc1, sc3, not_6_out, sc1, not_8_out);
  and and_20 (and_20_out, opc1, opc0, not_5_out, sc2, not_7_out, not_8_out);
  and and_21 (and_21_out, not_5_out, not_6_out, not_7_out, sc0);
  and and_22 (and_22_out, opc2, not_5_out, sc2, not_7_out, not_8_out);
  and and_23 (and_23_out, opc3, not_5_out, sc2, not_7_out, not_8_out);
  and and_24 (and_24_out, opc3, not_5_out, sc2, sc1, sc0);
  and and_25 (and_25_out, opc3, not_6_out, not_7_out, sc0);
  and and_26 (and_26_out, opc2, opc1, not_5_out, sc2, sc1, sc0);
  and and_27 (and_27_out, opc2, opc1, sc3, not_6_out, sc1, not_8_out);
  and and_28 (and_28_out, opc1, opc0, not_5_out, sc2, not_7_out, not_8_out);
  and and_29 (and_29_out, not_5_out, not_6_out, sc1, not_8_out);
  and and_30 (and_30_out, opc2, not_5_out, sc2, not_7_out, sc0);
  and and_31 (and_31_out, opc3, not_5_out, sc2, not_7_out, sc0);
  and and_32 (and_32_out, opc2, opc1, sc3, not_6_out, not_7_out, not_8_out);
  and and_33 (and_33_out, opc3, sc3, not_6_out, not_7_out, not_8_out);
  and and_34 (and_34_out, opc2, opc1, sc3, not_6_out, sc1, sc0);
  and and_35 (and_35_out, opc1, opc0, not_5_out, sc2, not_7_out, sc0);
  and and_36 (OR_MBR, opc3, sc3, not_6_out, sc1, not_8_out);
  and and_37 (WE_IR, not_5_out, not_6_out, sc1, not_8_out);
  and and_38 (and_38_out, not_5_out, not_6_out, not_7_out, not_8_out);
  and and_39 (and_39_out, opc2, not_5_out, not_6_out, sc1, sc0);
  and and_40 (and_40_out, opc3, not_5_out, not_6_out, sc1, sc0);
  and and_41 (and_41_out, opc3, not_5_out, sc2, sc1, not_8_out);
  and and_42 (and_42_out, opc3, sc3, not_6_out, not_7_out, sc0);
  and and_43 (and_43_out, opc2, opc1, not_5_out, sc2, sc1, not_8_out);
  and and_44 (and_44_out, opc2, opc1, sc3, not_6_out, not_7_out, sc0);
  and and_45 (and_45_out, opc1, opc0, not_5_out, not_6_out, sc1, sc0);
  and and_46 (and_46_out, not_5_out, not_6_out, not_7_out, sc0);
  and and_47 (and_47_out, opc2, not_5_out, sc2, not_7_out, not_8_out);
  and and_48 (and_48_out, opc3, not_5_out, sc2, not_7_out, not_8_out);
  and and_49 (and_49_out, opc3, not_5_out, sc2, sc1, sc0);
  and and_50 (and_50_out, opc3, sc3, not_6_out, sc1, not_8_out);
  and and_51 (and_51_out, opc2, opc1, not_5_out, sc2, sc1, sc0);
  and and_52 (and_52_out, opc2, opc1, sc3, not_6_out, sc1, not_8_out);
  and and_53 (and_53_out, opc1, opc0, not_5_out, sc2, not_7_out, not_8_out);
  and and_54 (OE_ALU, opc2, not_3_out, opc0, not_5_out, sc2, sc1, not_8_out);
  and and_55 (and_55_out, not_2_out, opc1, not_4_out, not_5_out, not_6_out, sc1, sc0);
  and and_56 (and_56_out, not_2_out, opc1, opc0, not_5_out, sc2, not_7_out, sc0);
  and and_57 (and_57_out, opc2, not_3_out, opc0, not_5_out, sc2, sc1, sc0);
  and and_58 (and_58_out, opc2, opc1, not_4_out, sc3, not_6_out, sc1, sc0);
  and and_59 (and_59_out, not_1_out, not_2_out, not_3_out, opc0, not_5_out, not_6_out, sc1, sc0);
  and and_60 (and_60_out, opc3, not_4_out, sc3, not_6_out, not_7_out, sc0);
  and and_61 (and_61_out, not_1_out, not_2_out, not_3_out, opc0, not_5_out, not_6_out, sc1, sc0);
  and and_62 (and_62_out, opc2, not_3_out, not_4_out, not_5_out, sc2, not_7_out, sc0);
  and and_63 (and_63_out, opc2, opc1, opc0, sc3, not_6_out, sc1, sc0);
  and and_64 (and_64_out, not_2_out, opc1, not_4_out, not_5_out, not_6_out, sc1, sc0);
  and and_65 (and_65_out, opc3, opc0, sc3, not_6_out, not_7_out, sc0);
  and and_66 (WE_OR, opc2, not_3_out, opc0, not_5_out, sc2, sc1, not_8_out);
  and and_67 (OE_OR, opc2, not_3_out, opc0, not_5_out, sc2, sc1, sc0);
  and and_68 (and_68_out, opc2, opc1, not_5_out, sc2, not_7_out, sc0);
  and and_69 (and_69_out, opc3, not_5_out, sc2, not_7_out, sc0);
  and and_70 (and_70_out, opc2, opc1, sc3, not_6_out, not_7_out, sc0);
  and and_71 (and_71_out, opc3, sc3, not_6_out, not_7_out, sc0);
  and and_72 (and_72_out, opc2, opc1, sc3, not_6_out, not_7_out, not_8_out);
  and and_73 (and_73_out, opc3, sc3, not_6_out, not_7_out, not_8_out);
  and and_74 (and_74_out, opc2, opc1, sc3, not_6_out, not_7_out, sc0);
  and and_75 (and_75_out, opc3, sc3, not_6_out, not_7_out, sc0);
  and and_76 (WE_VR, opc2, not_3_out, opc0, not_5_out, sc2, not_7_out, sc0);
  and and_77 (and_77_out, not_1_out, not_2_out, not_3_out, not_5_out, sc2, not_7_out, not_8_out);
  and and_78 (and_78_out, not_2_out, opc1, opc0, not_5_out, sc2, sc1, not_8_out);
  and and_79 (and_79_out, opc2, not_3_out, not_4_out, not_5_out, sc2, sc1, not_8_out);
  and and_80 (and_80_out, opc2, not_3_out, opc0, sc3, not_6_out, not_7_out, not_8_out);
  and and_81 (and_81_out, opc3, sc3, not_6_out, sc1, sc0);
  and and_82 (and_82_out, opc2, opc1, sc3, sc2, not_7_out, not_8_out);
  and and_83 (and_83_out, not_1_out, not_2_out, not_4_out, not_5_out, sc2, not_7_out, not_8_out);
  and and_84 (CLK_OFF, not_1_out, not_2_out, not_3_out, not_4_out, not_5_out, not_6_out, sc1, sc0);
  or or_1 (OE_PC, and_1_out, and_2_out, and_3_out, and_4_out, and_5_out, and_6_out);
  or or_2 (CE_PC, and_7_out, and_8_out, and_9_out, and_10_out, and_11_out, and_12_out);
  or or_3 (OE_RAM, and_14_out, and_15_out, and_16_out, and_17_out, and_18_out, and_19_out, and_20_out);
  or or_4 (WE_MBR, and_21_out, and_22_out, and_23_out, and_24_out, and_25_out, and_26_out, and_27_out, and_28_out);
  or or_5 (IOE_MBR, and_29_out, and_30_out, and_31_out, and_32_out, and_33_out, and_34_out, and_35_out);
  or or_6 (WE_MAR, and_38_out, and_39_out, and_40_out, and_41_out, and_42_out, and_43_out, and_44_out, and_45_out);
  or or_7 (OE_MAR, and_46_out, and_47_out, and_48_out, and_49_out, and_50_out, and_51_out, and_52_out, and_53_out);
  or or_8 (WE_RA, and_55_out, and_56_out, and_57_out, and_58_out);
  or or_9 (OE_RA, and_59_out, and_60_out);
  or or_10 (WE_RB, and_61_out, and_62_out, and_63_out);
  or or_11 (OE_RB, and_64_out, and_65_out);
  or or_12 (WE_ADDR0, and_68_out, and_69_out);
  or or_13 (OE_ADDR0, and_70_out, and_71_out);
  or or_14 (WE_ADDR1, and_72_out, and_73_out);
  or or_15 (OE_ADDR1, and_74_out, and_75_out);
  or or_16 (DONE_SC, and_77_out, and_78_out, and_79_out, and_80_out, and_81_out, and_82_out, and_83_out);

  assign OE_IR = 1'b0;
  assign OE_VR = 1'b0;
endmodule
