// Logisim project 8BItComputer_v4.0.circ as structural Verilog: 7 circuits, main circuit CPU
module CPU (
);

  wire and_1_out, and_2_out, CE_PC, CLK, CLK_OFF, clock_1_out, controlled_buffer_3_out, DEC_PC, DONE_SC,
       IOE_MBR, LD_PC, not_1_out, not_2_out, OE_ADDR0, OE_ADDR1, OE_ALU, OE_IR, OE_MAR, OE_MBR, OE_OR, OE_PC,
       OE_RA, OE_RAM, OE_RB, OE_VR, RESET, WE_ADDR0, WE_ADDR1, WE_IR, WE_MAR, WE_MBR, WE_OR, WE_RA, WE_RAM,
       WE_RB, WE_VR;
  wire [3:0] bitselector_1_out, SC;
  wire [7:0] ADDR0, ADDR1, ALU, EXT_DATA_BUS, IR, MBR, OR, RA, ram_1_dout, RB, rom_1_data, VR;
  wire [14:0] controlled_buffer_5_out;
  wire [15:0] EXT_ADDR_BUS, INT_ADDR_BUS, PC, register16bit_1_sd;
  wire [31:0] decimaldecoder_1_dout;

  MyRegister InstructionRegister (
    .OE(OE_IR), .WE(WE_IR), .Clock(CLK), .Reset(RESET), .Din(EXT_DATA_BUS), .StoredData(IR));  // open: Dout
  MyRegister RegisterA (
    .OE(OE_RA), .WE(WE_RA), .Clock(CLK), .Reset(RESET), .Din(EXT_DATA_BUS), .Dout(EXT_DATA_BUS),
    .StoredData(RA));
  MyRegister RegisterB (
    .OE(OE_RB), .WE(WE_RB), .Clock(CLK), .Reset(RESET), .Din(EXT_DATA_BUS), .Dout(EXT_DATA_BUS),
    .StoredData(RB));
  MyRegister Addr0Register (
    .OE(OE_ADDR0), .WE(WE_ADDR0), .Clock(CLK), .Reset(RESET), .Din(EXT_DATA_BUS), .Dout(INT_ADDR_BUS[7:0]),
    .StoredData(ADDR0));
  MyRegister Addr1Register (
    .OE(OE_ADDR1), .WE(WE_ADDR1), .Clock(CLK), .Reset(RESET), .Din(EXT_DATA_BUS), .Dout(INT_ADDR_BUS[15:8]),
    .StoredData(ADDR1));
  MyRegister ValueRegister (
    .OE(OE_VR), .WE(WE_VR), .Clock(CLK), .Reset(RESET), .Din(EXT_DATA_BUS), .Dout(EXT_DATA_BUS),
    .StoredData(VR));
  Hex_Digit_Display hex_digit_display_1 (.value(IR[7:4]));  // open: dp
  Hex_Digit_Display hex_digit_display_2 (.value(ADDR0[7:4]));  // open: dp
  Hex_Digit_Display hex_digit_display_3 (.value(ADDR1[7:4]));  // open: dp
  Hex_Digit_Display hex_digit_display_4 (.value(VR[7:4]));  // open: dp
  Hex_Digit_Display hex_digit_display_5 (.value(IR[3:0]));  // open: dp
  Hex_Digit_Display hex_digit_display_6 (.value(RA[7:4]));  // open: dp
  Hex_Digit_Display hex_digit_display_7 (.value(RA[3:0]));  // open: dp
  Hex_Digit_Display hex_digit_display_8 (.value(RB[7:4]));  // open: dp
  Hex_Digit_Display hex_digit_display_9 (.value(RB[3:0]));  // open: dp
  Hex_Digit_Display hex_digit_display_10 (.value(ADDR0[3:0]));  // open: dp
  Hex_Digit_Display hex_digit_display_11 (.value(ADDR1[3:0]));  // open: dp
  Hex_Digit_Display hex_digit_display_12 (.value(VR[3:0]));  // open: dp
  BitSelector #(.group(4)) bitselector_1 (.in(IR), .out(bitselector_1_out), .sel(1'b0));
  Hex_Digit_Display hex_digit_display_13 (.value(EXT_ADDR_BUS[15:12]));  // open: dp
  Hex_Digit_Display hex_digit_display_14 (.value(EXT_ADDR_BUS[11:8]));  // open: dp
  Hex_Digit_Display hex_digit_display_15 (.value(INT_ADDR_BUS[15:12]));  // open: dp
  Hex_Digit_Display hex_digit_display_16 (.value(INT_ADDR_BUS[11:8]));  // open: dp
  CU cu_1 (
    .opc1(bitselector_1_out[1]), .opc0(bitselector_1_out[0]), .sc3(SC[3]), .sc2(SC[2]), .sc1(SC[1]),
    .sc0(SC[0]), .opc3(bitselector_1_out[3]), .opc2(bitselector_1_out[2]), .DEC_PC(DEC_PC), .LD_PC(LD_PC),
    .WE_RAM(WE_RAM), .OE_RAM(OE_RAM), .WE_MBR(WE_MBR), .IOE_MBR(IOE_MBR), .OE_MBR(OE_MBR), .WE_IR(WE_IR),
    .OE_IR(OE_IR), .WE_MAR(WE_MAR), .OE_MAR(OE_MAR), .OE_ALU(OE_ALU), .WE_RA(WE_RA), .OE_RA(OE_RA),
    .WE_RB(WE_RB), .OE_RB(OE_RB), .OE_PC(OE_PC), .WE_OR(WE_OR), .OE_OR(OE_OR), .WE_ADDR0(WE_ADDR0),
    .OE_ADDR0(OE_ADDR0), .WE_ADDR1(WE_ADDR1), .OE_ADDR1(OE_ADDR1), .WE_VR(WE_VR), .OE_VR(OE_VR),
    .DONE_SC(DONE_SC), .CLK_OFF(CLK_OFF), .CE_PC(CE_PC));
  Hex_Digit_Display hex_digit_display_17 (.value(EXT_ADDR_BUS[7:4]));  // open: dp
  Hex_Digit_Display hex_digit_display_18 (.value(EXT_ADDR_BUS[3:0]));  // open: dp
  Hex_Digit_Display hex_digit_display_19 (.value(INT_ADDR_BUS[7:4]));  // open: dp
  Hex_Digit_Display hex_digit_display_20 (.value(INT_ADDR_BUS[3:0]));  // open: dp
  Hex_Digit_Display hex_digit_display_21 (.value(EXT_DATA_BUS[7:4]));  // open: dp
  Hex_Digit_Display hex_digit_display_22 (.value(EXT_DATA_BUS[3:0]));  // open: dp
  Hex_Digit_Display hex_digit_display_23 (.value(EXT_DATA_BUS[7:4]));  // open: dp
  Hex_Digit_Display hex_digit_display_24 (.value(EXT_DATA_BUS[3:0]));  // open: dp
  Clock clock_1 (.out(clock_1_out));
  Button button_1 (.out(RESET));
  not not_1 (not_1_out, CLK_OFF);
  assign CLK = not_1_out ? clock_1_out : 1'bz;  // Controlled_Buffer controlled_buffer_1
  Register16Bit register16bit_1 (
    .WE(WE_MAR), .OE(OE_MAR), .Clk(CLK), .Reset(RESET), .Din(INT_ADDR_BUS), .SD(register16bit_1_sd),
    .Dout(EXT_ADDR_BUS));
  Hex_Digit_Display hex_digit_display_25 (.value(register16bit_1_sd[15:12]));  // open: dp
  MyRegister u_MBR (
    .OE(OE_MBR), .WE(WE_MBR), .Clock(CLK), .Reset(RESET), .Din(EXT_DATA_BUS), .Dout(EXT_DATA_BUS),
    .StoredData(MBR));
  assign EXT_DATA_BUS = IOE_MBR ? MBR : 8'bz;  // Controlled_Buffer controlled_buffer_2
  MyRegister OutputRegister (
    .OE(OE_OR), .WE(WE_OR), .Clock(CLK), .Reset(RESET), .Din(EXT_DATA_BUS), .Dout(EXT_DATA_BUS),
    .StoredData(OR));
  assign controlled_buffer_3_out = not_2_out ? 1'b1 : 1'bz;  // Controlled_Buffer controlled_buffer_3
  not not_2 (not_2_out, DEC_PC);
  Hex_Digit_Display hex_digit_display_26 (.value(register16bit_1_sd[11:8]));  // open: dp
  Hex_Digit_Display hex_digit_display_27 (.value(register16bit_1_sd[7:4]));  // open: dp
  Counter #(.max('hffff), .width(16)) ProgramCounter (
    .clr(RESET), .load(LD_PC), .up(controlled_buffer_3_out), .count(CE_PC), .clk(CLK), .D(INT_ADDR_BUS),
    .Q(PC));  // open: carry
  Counter #(.max('hf), .width(4)) Step_Counter_4e214656 (
    .clr(RESET), .load(DONE_SC), .up(1'b1), .count(1'b1), .clk(CLK), .D(4'b0000), .Q(SC));  // open: carry
  Hex_Digit_Display hex_digit_display_28 (.value(register16bit_1_sd[3:0]));  // open: dp
  Hex_Digit_Display hex_digit_display_29 (.value(MBR[7:4]));  // open: dp
  Hex_Digit_Display hex_digit_display_30 (.value(MBR[3:0]));  // open: dp
  Hex_Digit_Display hex_digit_display_31 (.value(OR[7:4]));  // open: dp
  Hex_Digit_Display hex_digit_display_32 (.value(OR[3:0]));  // open: dp
  Hex_Digit_Display hex_digit_display_33 (.value(ALU[7:4]));  // open: dp
  assign INT_ADDR_BUS = OE_PC ? PC : 16'bz;  // Controlled_Buffer controlled_buffer_4
  Hex_Digit_Display hex_digit_display_34 (.value(SC));  // open: dp
  Hex_Digit_Display hex_digit_display_35 (.value(ALU[3:0]));  // open: dp
  ALUs alus_1 (.OE(OE_ALU), .Reg_B(VR), .Reg_A(RA), .ALU_Result(ALU), .Dout(EXT_DATA_BUS));  // open: Carry_Out
  DecimalDecoder decimaldecoder_1 (.Din(ALU), .Dout(decimaldecoder_1_dout));
  _7_Segment_Display u_7_segment_display_1 (
    .g(decimaldecoder_1_dout[15]), .f(decimaldecoder_1_dout[14]), .a(decimaldecoder_1_dout[13]),
    .b(decimaldecoder_1_dout[12]), .e(decimaldecoder_1_dout[31]), .d(decimaldecoder_1_dout[30]),
    .c(decimaldecoder_1_dout[29]), .dp(decimaldecoder_1_dout[28]));
  ROM #(.addrWidth(15)) rom_1 (.addr(EXT_ADDR_BUS[14:0]), .data(rom_1_data));
  _7_Segment_Display u_7_segment_display_2 (
    .g(decimaldecoder_1_dout[11]), .f(decimaldecoder_1_dout[10]), .a(decimaldecoder_1_dout[9]),
    .b(decimaldecoder_1_dout[8]), .e(decimaldecoder_1_dout[27]), .d(decimaldecoder_1_dout[26]),
    .c(decimaldecoder_1_dout[25]), .dp(decimaldecoder_1_dout[24]));
  _7_Segment_Display u_7_segment_display_3 (
    .g(decimaldecoder_1_dout[7]), .f(decimaldecoder_1_dout[6]), .a(decimaldecoder_1_dout[5]),
    .b(decimaldecoder_1_dout[4]), .e(decimaldecoder_1_dout[23]), .d(decimaldecoder_1_dout[22]),
    .c(decimaldecoder_1_dout[21]), .dp(decimaldecoder_1_dout[20]));
  _7_Segment_Display u_7_segment_display_4 (
    .g(decimaldecoder_1_dout[3]), .f(decimaldecoder_1_dout[2]), .a(decimaldecoder_1_dout[1]),
    .b(decimaldecoder_1_dout[0]), .e(decimaldecoder_1_dout[19]), .d(decimaldecoder_1_dout[18]),
    .c(decimaldecoder_1_dout[17]), .dp(decimaldecoder_1_dout[16]));
  assign controlled_buffer_5_out = EXT_ADDR_BUS[15] ? EXT_ADDR_BUS[14:0] : 15'bz;  // Controlled_Buffer controlled_buffer_5
  assign EXT_DATA_BUS = and_1_out ? rom_1_data : 8'bz;  // Controlled_Buffer controlled_buffer_6
  and and_1 (and_1_out, OE_RAM, ~EXT_ADDR_BUS[15]);  // AND_Gate
  RAM #(.addrWidth(15), .enables("line")) ram_1 (
    .addr(controlled_buffer_5_out), .we(WE_RAM), .clk(CLK), .din(EXT_DATA_BUS), .dout(ram_1_dout));
  assign EXT_DATA_BUS = and_2_out ? ram_1_dout : 8'bz;  // Controlled_Buffer controlled_buffer_7
  and and_2 (and_2_out, OE_RAM, EXT_ADDR_BUS[15]);

  // Other names for the same wires on the sheet: INT_DATA_BUS[7:0] = EXT_DATA_BUS

  // Notes on the sheet:
  //   Instruction Register
  //   Register A
  //   Register B
  //   Addr1Register
  //   External Address Bus
  //   Internal Address Bus
  //   Internal Data Bus
  //   External Data Bus
  //   MAR
  //   MBR
  //   Output Register
  //   Program Counter
  //   Step Counter
  //   contents of rom_1 (hex, n*v repeats v):
  //   3 aa 8 0 80 7 0 80 3 11 a 0 80 8 1 80
  //   PROGRAM
  //   MEMORY
  //   BARIABELS
endmodule

module MemoryCell (
  input  Clock,
  input  WE,
  input  Din,
  input  OE,
  input  Reset,
  output Dout,
  output StoredData
);

  wire and_1_out, and_2_out, not_1_out, or_1_out;

  not not_1 (not_1_out, WE);
  and and_1 (and_1_out, StoredData, not_1_out);
  and and_2 (and_2_out, WE, Din);
  or or_1 (or_1_out, and_1_out, and_2_out);
  D_Flip_Flop d_ff_1 (.D(or_1_out), .clk(Clock), .Q(StoredData), .reset(Reset));  // open: Qn, preset
  assign Dout = OE ? StoredData : 1'bz;  // Controlled_Buffer controlled_buffer_1
endmodule

module MyRegister (
  input  Reset,
  input  OE,
  input  [7:0] Din,
  input  WE,
  input  Clock,
  output [7:0] Dout,
  output [7:0] StoredData
);

  MemoryCell R0 (
    .WE(WE), .Din(Din[0]), .OE(OE), .Reset(Reset), .Clock(Clock), .Dout(Dout[0]), .StoredData(StoredData[0]));
  MemoryCell R1 (
    .WE(WE), .Din(Din[1]), .OE(OE), .Reset(Reset), .Clock(Clock), .Dout(Dout[1]), .StoredData(StoredData[1]));
  MemoryCell R2 (
    .WE(WE), .Din(Din[2]), .OE(OE), .Clock(Clock), .Dout(Dout[2]), .StoredData(StoredData[2]));  // open: Reset
  MemoryCell memorycell_1 (
    .WE(WE), .Din(Din[3]), .OE(OE), .Reset(Reset), .Clock(Clock), .Dout(Dout[3]), .StoredData(StoredData[3]));
  MemoryCell R (
    .WE(WE), .Din(Din[4]), .OE(OE), .Reset(Reset), .Clock(Clock), .Dout(Dout[4]), .StoredData(StoredData[4]));
  MemoryCell R5 (
    .WE(WE), .Din(Din[5]), .OE(OE), .Reset(Reset), .Clock(Clock), .Dout(Dout[5]), .StoredData(StoredData[5]));
  MemoryCell R6 (
    .WE(WE), .Din(Din[6]), .OE(OE), .Reset(Reset), .Clock(Clock), .Dout(Dout[6]), .StoredData(StoredData[6]));
  MemoryCell R7 (
    .WE(WE), .Din(Din[7]), .OE(OE), .Reset(Reset), .Clock(Clock), .Dout(Dout[7]), .StoredData(StoredData[7]));
endmodule

module ALUs (
  input  [7:0] Reg_A,
  input  [7:0] Reg_B,
  input  OE,
  output [7:0] Dout,
  output [7:0] ALU_Result,
  output Carry_Out
);

  Adder adder_1 (.a(Reg_A), .b(Reg_B), .out(ALU_Result), .cout(Carry_Out));  // open: cin
  assign Dout = OE ? ALU_Result : 8'bz;  // Controlled_Buffer controlled_buffer_1

  // Notes on the sheet:
  //   ALU (8Bit)
endmodule

module DecimalDecoder (
  input  [7:0] Din,
  output [31:0] Dout
);

  ROM #(.dataWidth(32)) rom_1 (
    .addr(Din),
    .data({Dout[31:28], Dout[15:12], Dout[27:24], Dout[11:8], Dout[23:20], Dout[7:4], Dout[19:16], Dout[3:0]}));

  // Notes on the sheet:
  //   contents of rom_1 (hex, n*v repeats v):
  //   e7 21 cb 6b 2d 6e ee 23 ef 2f 21e7 2121 21cb 216b 212d 216e 21ee 2123 21ef 212f cbe7 cb21 cbcb cb6b
  //   cb2d cb6e cbee cb23 cbef cb2f 6be7 6b21 6bcb 6b6b 6b2d 6b6e 6bee 6b23 6bef 6b2f 2de7 2d21 2dcb 2d6b
  //   2d2d 2d6e 2dee 2d23 2def 2d2f 6ee7 6e21 6ecb 6e6b 6e2d 6e6e 6eee 6e23 6eef 6e2f eee7 ee21 eecb ee6b
  //   ee2d ee6e eeee ee23 eeef ee2f 23e7 2321 23cb 236b 232d 236e 23ee 2323 23ef 232f efe7 ef21 efcb ef6b
  //   ef2d ef6e efee ef23 efef ef2f 2fe7 2f21 2fcb 2f6b 2f2d 2f6e 2fee 2f23 2fef 2f2f 21e7e7 21e721 21e7cb
  //   21e76b 21e72d 21e76e 21e7ee 21e723 21e7ef 21e72f 2121e7 212121 2121cb 21216b 21212d 21216e 2121ee
  //   212123 2121ef 21212f 21cbe7 21cb21 21cbcb 21cb6b 21cb2d 21cb6e 21cbee 21cb23 21cbef 21cb2f 216be7
  //   216b21 216bcb 216b6b 216b2d 216b6e 216bee 216b23 216bef 216b2f 212de7 212d21 212dcb 212d6b 212d2d
  //   212d6e 212dee 212d23 212def 212d2f 216ee7 216e21 216ecb 216e6b 216e2d 216e6e 216eee 216e23 216eef
  //   216e2f 21eee7 21ee21 21eecb 21ee6b 21ee2d 21ee6e 21eeee 21ee23 21eeef 21ee2f 2123e7 212321 2123cb
  //   21236b 21232d 21236e 2123ee 212323 2123ef 21232f 21efe7 21ef21 21efcb 21ef6b 21ef2d 21ef6e 21efee
  //   21ef23 21efef 21ef2f 212fe7 212f21 212fcb 212f6b 212f2d 212f6e 212fee 212f23 212fef 212f2f cbe7e7
  //   cbe721 cbe7cb cbe76b cbe72d cbe76e cbe7ee cbe723 cbe7ef cbe72f cb21e7 cb2121 cb21cb cb216b cb212d
  //   cb216e cb21ee cb2123 cb21ef cb212f cbcbe7 cbcb21 cbcbcb cbcb6b cbcb2d cbcb6e cbcbee cbcb23 cbcbef
  //   cbcb2f cb6be7 cb6b21 cb6bcb cb6b6b cb6b2d cb6b6e cb6bee cb6b23 cb6bef cb6b2f cb2de7 cb2d21 cb2dcb
  //   cb2d6b cb2d2d cb2d6e cb2dee cb2d23 cb2def cb2d2f cb6ee7 cb6e21 cb6ecb cb6e6b cb6e2d cb6e6e
endmodule

module Register16Bit (
  input  [15:0] Din,
  input  OE,
  input  WE,
  input  Clk,
  input  Reset,
  output [15:0] Dout,
  output [15:0] SD
);

  MyRegister myregister_1 (
    .OE(OE), .WE(WE), .Clock(Clk), .Reset(Reset), .Din(Din[7:0]), .Dout(Dout[7:0]), .StoredData(SD[7:0]));
  MyRegister myregister_2 (
    .OE(OE), .WE(WE), .Clock(Clk), .Reset(Reset), .Din(Din[15:8]), .Dout(Dout[15:8]), .StoredData(SD[15:8]));
endmodule

module CU (
  input  opc3,
  input  opc2,
  input  opc1,
  input  opc0,
  input  sc3,
  input  sc2,
  input  sc1,
  input  sc0,
  output OE_PC,
  output CE_PC,
  output DEC_PC,
  output LD_PC,
  output WE_RAM,
  output OE_RAM,
  output WE_MBR,
  output IOE_MBR,
  output OE_MBR,
  output WE_IR,
  output OE_IR,
  output WE_MAR,
  output OE_MAR,
  output OE_ALU,
  output WE_RA,
  output OE_RA,
  output WE_RB,
  output OE_RB,
  output WE_OR,
  output OE_OR,
  output WE_ADDR0,
  output OE_ADDR0,
  output WE_ADDR1,
  output OE_ADDR1,
  output WE_VR,
  output OE_VR,
  output DONE_SC,
  output CLK_OFF
);

  wire and_1_out, and_2_out, and_3_out, and_4_out, and_5_out, and_6_out, and_7_out, and_8_out, and_9_out,
       and_10_out, and_11_out, and_12_out, and_14_out, and_15_out, and_16_out, and_17_out, and_18_out,
       and_19_out, and_20_out, and_21_out, and_22_out, and_23_out, and_24_out, and_25_out, and_26_out,
       and_27_out, and_28_out, and_29_out, and_30_out, and_31_out, and_32_out, and_33_out, and_34_out,
       and_35_out, and_36_out, and_37_out, and_38_out, and_41_out, and_42_out, and_43_out, and_44_out,
       and_45_out, and_46_out, and_47_out, and_48_out, and_49_out, and_50_out, and_51_out, and_52_out,
       and_53_out, and_54_out, and_55_out, and_56_out, and_57_out, and_58_out, and_59_out, and_60_out,
       and_61_out, and_62_out, and_63_out, and_64_out, and_65_out, and_66_out, and_67_out, and_68_out,
       and_69_out, and_70_out, and_71_out, and_72_out, and_73_out, and_74_out, and_75_out, and_76_out,
       and_77_out, and_78_out, and_79_out, and_80_out, and_81_out, and_82_out, and_83_out, and_84_out,
       and_85_out, and_86_out, and_87_out, and_88_out, and_89_out, and_90_out, and_91_out, and_92_out,
       not_1_out, not_2_out, not_3_out, not_4_out, not_5_out, not_6_out, not_7_out, not_8_out;

  not not_1 (not_1_out, opc3);
  not not_2 (not_2_out, opc2);
  not not_3 (not_3_out, opc1);
  not not_4 (not_4_out, opc0);
  not not_5 (not_5_out, sc3);
  not not_6 (not_6_out, sc2);
  not not_7 (not_7_out, sc1);
  not not_8 (not_8_out, sc0);
  and and_1 (and_1_out, not_5_out, not_6_out, not_7_out, not_8_out);
  and and_2 (and_2_out, opc2, not_5_out, not_6_out, sc1, sc0);
  and and_3 (and_3_out, opc3, not_5_out, not_6_out, sc1, sc0);
  and and_4 (and_4_out, opc2, opc1, not_5_out, sc2, sc1, not_8_out);
  and and_5 (and_5_out, opc3, not_5_out, sc2, sc1, not_8_out);
  and and_6 (and_6_out, opc1, opc0, not_5_out, not_6_out, sc1, sc0);
  and and_7 (and_7_out, not_5_out, not_6_out, not_7_out, sc0);
  and and_8 (and_8_out, opc2, not_5_out, sc2, not_7_out, not_8_out);
  and and_9 (and_9_out, opc3, not_5_out, sc2, not_7_out, not_8_out);
  and and_10 (and_10_out, opc2, opc1, not_5_out, sc2, sc1, sc0);
  and and_11 (and_11_out, opc3, not_5_out, sc2, sc1, sc0);
  and and_12 (and_12_out, opc1, opc0, not_5_out, sc2, not_7_out, not_8_out);
  and and_13 (WE_RAM, opc3, not_3_out, sc3, not_6_out, sc1, not_8_out);
  and and_14 (and_14_out, not_5_out, not_6_out, not_7_out, sc0);
  and and_15 (and_15_out, opc2, not_5_out, sc2, not_7_out, not_8_out);
  and and_16 (and_16_out, opc3, not_5_out, sc2, not_7_out, not_8_out);
  and and_17 (and_17_out, opc3, not_5_out, sc2, sc1, sc0);
  and and_18 (and_18_out, opc2, opc1, not_5_out, sc2, sc1, sc0);
  and and_19 (and_19_out, opc2, opc1, sc3, not_6_out, sc1, not_8_out);
  and and_20 (and_20_out, opc3, opc1, sc3, not_6_out, sc1, not_8_out);
  and and_21 (and_21_out, opc1, opc0, not_5_out, sc2, not_7_out, not_8_out);
  and and_22 (and_22_out, not_5_out, not_6_out, not_7_out, sc0);
  and and_23 (and_23_out, opc2, not_5_out, sc2, not_7_out, not_8_out);
  and and_24 (and_24_out, opc3, not_5_out, sc2, not_7_out, not_8_out);
  and and_25 (and_25_out, opc3, not_5_out, sc2, sc1, sc0);
  and and_26 (and_26_out, opc3, not_3_out, not_6_out, not_7_out, sc0);
  and and_27 (and_27_out, opc2, opc1, not_5_out, sc2, sc1, sc0);
  and and_28 (and_28_out, opc2, opc1, sc3, not_6_out, sc1, not_8_out);
  and and_29 (and_29_out, opc3, opc1, sc3, not_6_out, sc1, not_8_out);
  and and_30 (and_30_out, opc1, opc0, not_5_out, sc2, not_7_out, not_8_out);
  and and_31 (and_31_out, not_5_out, not_6_out, sc1, not_8_out);
  and and_32 (and_32_out, opc2, not_5_out, sc2, not_7_out, sc0);
  and and_33 (and_33_out, opc3, not_5_out, sc2, not_7_out, sc0);
  and and_34 (and_34_out, opc3, sc3, not_6_out, not_7_out, not_8_out);
  and and_35 (and_35_out, opc2, opc1, sc3, not_6_out, not_7_out, not_8_out);
  and and_36 (and_36_out, opc2, opc1, sc3, not_6_out, sc1, sc0);
  and and_37 (and_37_out, opc3, opc1, sc3, not_6_out, sc1, sc0);
  and and_38 (and_38_out, opc1, opc0, not_5_out, sc2, not_7_out, sc0);
  and and_39 (OE_MBR, opc3, not_3_out, sc3, not_6_out, sc1, not_8_out);
  and and_40 (WE_IR, not_5_out, not_6_out, sc1, not_8_out);
  and and_41 (and_41_out, not_5_out, not_6_out, not_7_out, not_8_out);
  and and_42 (and_42_out, opc2, not_5_out, not_6_out, sc1, sc0);
  and and_43 (and_43_out, opc3, not_5_out, not_6_out, sc1, sc0);
  and and_44 (and_44_out, opc3, not_5_out, sc2, sc1, not_8_out);
  and and_45 (and_45_out, opc3, sc3, not_6_out, not_7_out, sc0);
  and and_46 (and_46_out, opc2, opc1, not_5_out, sc2, sc1, not_8_out);
  and and_47 (and_47_out, opc2, opc1, sc3, not_6_out, not_7_out, sc0);
  and and_48 (and_48_out, opc1, opc0, not_5_out, not_6_out, sc1, sc0);
  and and_49 (and_49_out, not_5_out, not_6_out, not_7_out, sc0);
  and and_50 (and_50_out, opc2, not_5_out, sc2, not_7_out, not_8_out);
  and and_51 (and_51_out, opc3, not_5_out, sc2, not_7_out, not_8_out);
  and and_52 (and_52_out, opc3, not_5_out, sc2, sc1, sc0);
  and and_53 (and_53_out, opc3, sc3, not_6_out, sc1, not_8_out);
  and and_54 (and_54_out, opc2, opc1, not_5_out, sc2, sc1, sc0);
  and and_55 (and_55_out, opc2, opc1, sc3, not_6_out, sc1, not_8_out);
  and and_56 (and_56_out, opc1, opc0, not_5_out, sc2, not_7_out, not_8_out);
  and and_57 (and_57_out, opc2, not_3_out, opc0, not_5_out, sc2, sc1, not_8_out);
  and and_58 (and_58_out, opc3, opc1, sc3, sc2, not_7_out, not_8_out);
  and and_59 (and_59_out, not_1_out, not_2_out, opc1, not_4_out, not_5_out, not_6_out, sc1, sc0);
  and and_60 (and_60_out, not_2_out, opc1, opc0, not_5_out, sc2, not_7_out, sc0);
  and and_61 (and_61_out, opc2, not_3_out, opc0, not_5_out, sc2, sc1, sc0);
  and and_62 (and_62_out, opc2, opc1, not_4_out, sc3, not_6_out, sc1, sc0);
  and and_63 (and_63_out, opc3, opc1, sc3, sc2, not_7_out, sc0);
  and and_64 (and_64_out, not_1_out, not_2_out, not_3_out, opc0, not_5_out, not_6_out, sc1, sc0);
  and and_65 (and_65_out, opc3, not_3_out, not_4_out, sc3, not_6_out, not_7_out, sc0);
  and and_66 (and_66_out, not_1_out, not_2_out, not_3_out, opc0, not_5_out, not_6_out, sc1, sc0);
  and and_67 (and_67_out, opc2, not_3_out, not_4_out, not_5_out, sc2, not_7_out, sc0);
  and and_68 (and_68_out, opc2, opc1, opc0, sc3, not_6_out, sc1, sc0);
  and and_69 (and_69_out, not_1_out, not_2_out, opc1, not_4_out, not_5_out, not_6_out, sc1, sc0);
  and and_70 (and_70_out, opc3, opc0, sc3, not_6_out, not_7_out, sc0);
  and and_71 (and_71_out, opc2, not_3_out, opc0, not_5_out, sc2, sc1, not_8_out);
  and and_72 (and_72_out, opc3, opc1, sc3, sc2, not_7_out, not_8_out);
  and and_73 (and_73_out, opc2, not_3_out, opc0, not_5_out, sc2, sc1, sc0);
  and and_74 (and_74_out, opc3, opc1, sc3, sc2, not_7_out, sc0);
  and and_75 (and_75_out, opc2, opc1, not_5_out, sc2, not_7_out, sc0);
  and and_76 (and_76_out, opc3, not_5_out, sc2, not_7_out, sc0);
  and and_77 (and_77_out, opc2, opc1, sc3, not_6_out, not_7_out, sc0);
  and and_78 (and_78_out, opc3, sc3, not_6_out, not_7_out, sc0);
  and and_79 (and_79_out, opc2, opc1, sc3, not_6_out, not_7_out, not_8_out);
  and and_80 (and_80_out, opc3, sc3, not_6_out, not_7_out, not_8_out);
  and and_81 (and_81_out, opc2, opc1, sc3, not_6_out, not_7_out, sc0);
  and and_82 (and_82_out, opc3, sc3, not_6_out, not_7_out, sc0);
  and and_83 (and_83_out, opc2, not_3_out, opc0, not_5_out, sc2, not_7_out, sc0);
  and and_84 (and_84_out, opc3, opc1, sc3, not_6_out, sc1, sc0);
  and and_85 (and_85_out, not_1_out, not_2_out, not_3_out, not_5_out, sc2, not_7_out, not_8_out);
  and and_86 (and_86_out, not_1_out, not_2_out, not_4_out, not_5_out, sc2, not_7_out, not_8_out);
  and and_87 (and_87_out, not_2_out, opc1, opc0, not_5_out, sc2, sc1, not_8_out);
  and and_88 (and_88_out, opc2, not_3_out, not_4_out, not_5_out, sc2, sc1, not_8_out);
  and and_89 (and_89_out, opc2, not_3_out, opc0, sc3, not_6_out, not_7_out, not_8_out);
  and and_90 (and_90_out, opc3, not_3_out, sc3, not_6_out, sc1, sc0);
  and and_91 (and_91_out, opc2, opc1, sc3, sc2, not_7_out, not_8_out);
  and and_92 (and_92_out, opc3, opc1, sc3, sc2, sc1, not_8_out);
  and and_93 (CLK_OFF, not_1_out, not_2_out, not_3_out, not_4_out, not_5_out, not_6_out, sc1, sc0);
  or or_1 (OE_PC, and_1_out, and_2_out, and_3_out, and_4_out, and_5_out, and_6_out);
  or or_2 (CE_PC, and_7_out, and_8_out, and_9_out, and_10_out, and_11_out, and_12_out);
  or or_3 (OE_RAM, and_14_out, and_15_out, and_16_out, and_17_out, and_18_out, and_19_out, and_20_out, and_21_out);
  or or_4 (WE_MBR, and_22_out, and_23_out, and_24_out, and_25_out, and_26_out, and_27_out, and_28_out, and_29_out, and_30_out);
  or or_5 (IOE_MBR, and_31_out, and_32_out, and_33_out, and_34_out, and_35_out, and_36_out, and_37_out, and_38_out);
  or or_6 (WE_MAR, and_41_out, and_42_out, and_43_out, and_44_out, and_45_out, and_46_out, and_47_out, and_48_out);
  or or_7 (OE_MAR, and_49_out, and_50_out, and_51_out, and_52_out, and_53_out, and_54_out, and_55_out, and_56_out);
  or or_8 (OE_ALU, and_57_out, and_58_out);
  or or_9 (WE_RA, and_59_out, and_60_out, and_61_out, and_62_out, and_63_out);
  or or_10 (OE_RA, and_64_out, and_65_out);
  or or_11 (WE_RB, and_66_out, and_67_out, and_68_out);
  or or_12 (OE_RB, and_69_out, and_70_out);
  or or_13 (WE_OR, and_71_out, and_72_out);
  or or_14 (OE_OR, and_73_out, and_74_out);
  or or_15 (WE_ADDR0, and_75_out, and_76_out);
  or or_16 (OE_ADDR0, and_77_out, and_78_out);
  or or_17 (WE_ADDR1, and_79_out, and_80_out);
  or or_18 (OE_ADDR1, and_81_out, and_82_out);
  or or_19 (WE_VR, and_83_out, and_84_out);
  or or_20 (DONE_SC, and_85_out, and_86_out, and_87_out, and_88_out, and_89_out, and_90_out, and_91_out, and_92_out);

  assign DEC_PC = 1'b0;
  assign LD_PC = 1'b0;
  assign OE_IR = 1'b0;
  assign OE_VR = 1'b0;
endmodule
