// Logisim project 8BItComputer_v6.0.circ as structural Verilog
module CPU (
);

  wire and_1_out, and_2_out, CE_PC, CLK, CLK_OFF, clock_1_out, controlled_buffer_5_out, DEC_PC, DONE_SC,
       IOE_MBR, LD_PC, not_1_out, not_2_out, OE_ADDR0, OE_ADDR1, OE_ADDR2, OE_ADDR3, OE_ALU, OE_IR, OE_MAR,
       OE_MBR, OE_OR, OE_PC, OE_RA, OE_RAM, OE_RB, OE_TV0, OE_TV1, or_1_out, or_2_out, R_ADDR1, R_ADDR3,
       RESET, WE_ADDR0, WE_ADDR1, WE_ADDR2, WE_ADDR3, WE_IR, WE_MAR, WE_MBR, WE_OR, WE_RA, WE_RAM, WE_RB,
       WE_TV0, WE_TV1;
  wire [2:0] OP;
  wire [7:0] ADDR0, ADDR1, ADDR2, ADDR3, EXT_DATA_BUS, IR, MBR, MyALU_alu_result, OR, RA, ram_1_dout, RB,
       rom_1_data, SC, TV0, TV1, VR;
  wire [14:0] controlled_buffer_2_out;
  wire [15:0] EXT_ADDR_BUS, INT_ADDR_BUS, MAR_sd, PC;

  or or_1 (or_1_out, RESET, R_ADDR1);
  MyRegister InstructionRegister (
    .OE(OE_IR), .WE(WE_IR), .Clock(CLK), .Reset(RESET), .Din(EXT_DATA_BUS), .StoredData(IR));  // open: Dout
  MyRegister RegisterA (
    .OE(OE_RA), .WE(WE_RA), .Clock(CLK), .Reset(RESET), .Din(EXT_DATA_BUS), .Dout(EXT_DATA_BUS),
    .StoredData(RA));
  MyRegister RegisterB (
    .OE(OE_RB), .WE(WE_RB), .Clock(CLK), .Reset(RESET), .Din(EXT_DATA_BUS), .Dout(EXT_DATA_BUS),
    .StoredData(RB));
  MyRegister Addr0Register (
    .OE(OE_ADDR0), .WE(WE_ADDR0), .Clock(CLK), .Reset(RESET), .Din(EXT_DATA_BUS), .Dout(INT_ADDR_BUS[7:0]),
    .StoredData(ADDR0));
  MyRegister Addr1Register (
    .OE(OE_ADDR1), .WE(WE_ADDR1), .Clock(CLK), .Reset(or_1_out), .Din(EXT_DATA_BUS),
    .Dout(INT_ADDR_BUS[15:8]), .StoredData(ADDR1));
  MyRegister myregister_1 (
    .OE(OE_TV1), .WE(WE_TV1), .Clock(CLK), .Reset(RESET), .Din(EXT_DATA_BUS), .Dout(EXT_DATA_BUS),
    .StoredData(TV1));
  Hex_Digit_Display hex_digit_display_1 (.value(IR[7:4]));  // open: dp
  MyRegister ValueRegister (
    .OE(OE_TV0), .WE(WE_TV0), .Clock(CLK), .Reset(RESET), .Din(EXT_DATA_BUS), .Dout(EXT_DATA_BUS),
    .StoredData(TV0));
  MyRegister myregister_2 (
    .OE(OE_ADDR2), .WE(WE_ADDR2), .Clock(CLK), .Reset(RESET), .Din(EXT_DATA_BUS), .Dout(INT_ADDR_BUS[7:0]),
    .StoredData(ADDR2));
  or or_2 (or_2_out, RESET, R_ADDR3);
  Hex_Digit_Display hex_digit_display_2 (.value(TV1[7:4]));  // open: dp
  Hex_Digit_Display hex_digit_display_3 (.value(IR[3:0]));  // open: dp
  Hex_Digit_Display hex_digit_display_4 (.value(RA[7:4]));  // open: dp
  Hex_Digit_Display hex_digit_display_5 (.value(RA[3:0]));  // open: dp
  Hex_Digit_Display hex_digit_display_6 (.value(RB[7:4]));  // open: dp
  Hex_Digit_Display hex_digit_display_7 (.value(RB[3:0]));  // open: dp
  Hex_Digit_Display hex_digit_display_8 (.value(ADDR0[7:4]));  // open: dp
  Hex_Digit_Display hex_digit_display_9 (.value(ADDR0[3:0]));  // open: dp
  Hex_Digit_Display hex_digit_display_10 (.value(ADDR1[7:4]));  // open: dp
  Hex_Digit_Display hex_digit_display_11 (.value(ADDR1[3:0]));  // open: dp
  Hex_Digit_Display hex_digit_display_12 (.value(TV0[7:4]));  // open: dp
  MyRegister myregister_3 (
    .OE(OE_ADDR3), .WE(WE_ADDR3), .Clock(CLK), .Reset(or_2_out), .Din(EXT_DATA_BUS),
    .Dout(INT_ADDR_BUS[15:8]), .StoredData(ADDR3));
  Hex_Digit_Display hex_digit_display_13 (.value(TV1[3:0]));  // open: dp
  Hex_Digit_Display hex_digit_display_14 (.value(TV0[3:0]));  // open: dp
  Hex_Digit_Display hex_digit_display_15 (.value(ADDR2[7:4]));  // open: dp
  Hex_Digit_Display hex_digit_display_16 (.value(ADDR2[3:0]));  // open: dp
  Hex_Digit_Display hex_digit_display_17 (.value(ADDR3[7:4]));  // open: dp
  Hex_Digit_Display hex_digit_display_18 (.value(ADDR3[3:0]));  // open: dp
  Hex_Digit_Display hex_digit_display_19 (.value(EXT_ADDR_BUS[15:12]));  // open: dp
  Hex_Digit_Display hex_digit_display_20 (.value(EXT_ADDR_BUS[11:8]));  // open: dp
  Hex_Digit_Display hex_digit_display_21 (.value(INT_ADDR_BUS[15:12]));  // open: dp
  Hex_Digit_Display hex_digit_display_22 (.value(INT_ADDR_BUS[11:8]));  // open: dp
  Hex_Digit_Display hex_digit_display_23 (.value(EXT_ADDR_BUS[7:4]));  // open: dp
  Hex_Digit_Display hex_digit_display_24 (.value(EXT_ADDR_BUS[3:0]));  // open: dp
  Hex_Digit_Display hex_digit_display_25 (.value(INT_ADDR_BUS[7:4]));  // open: dp
  Hex_Digit_Display hex_digit_display_26 (.value(INT_ADDR_BUS[3:0]));  // open: dp
  Hex_Digit_Display hex_digit_display_27 (.value(EXT_DATA_BUS[7:4]));  // open: dp
  Hex_Digit_Display hex_digit_display_28 (.value(EXT_DATA_BUS[3:0]));  // open: dp
  Hex_Digit_Display hex_digit_display_29 (.value(EXT_DATA_BUS[7:4]));  // open: dp
  Hex_Digit_Display hex_digit_display_30 (.value(EXT_DATA_BUS[3:0]));  // open: dp
  Clock clock_1 (.out(clock_1_out));
  Button button_1 (.out(RESET));
  not not_1 (not_1_out, CLK_OFF);
  assign CLK = not_1_out ? clock_1_out : 1'bz;  // Controlled_Buffer controlled_buffer_1
  ROM #(.addrWidth(15)) rom_1 (.addr(EXT_ADDR_BUS[14:0]), .data(rom_1_data));
  Register16Bit MAR (
    .WE(WE_MAR), .OE(OE_MAR), .Clk(CLK), .Reset(RESET), .Din(INT_ADDR_BUS), .SD(MAR_sd), .Dout(EXT_ADDR_BUS));
  Hex_Digit_Display hex_digit_display_31 (.value(MAR_sd[15:12]));  // open: dp
  Hex_Digit_Display hex_digit_display_32 (.value(MAR_sd[11:8]));  // open: dp
  Hex_Digit_Display hex_digit_display_33 (.value(MAR_sd[7:4]));  // open: dp
  assign controlled_buffer_2_out = EXT_ADDR_BUS[15] ? EXT_ADDR_BUS[14:0] : 15'bz;  // Controlled_Buffer controlled_buffer_2
  assign EXT_DATA_BUS = and_1_out ? rom_1_data : 8'bz;  // Controlled_Buffer controlled_buffer_3
  Hex_Digit_Display hex_digit_display_34 (.value(MAR_sd[3:0]));  // open: dp
  and and_1 (and_1_out, OE_RAM, ~EXT_ADDR_BUS[15]);  // AND_Gate
  CU cu_1 ();  // open: opc2, opc1, opc0, sc3, sc2, sc1, sc0, opc4, opc3, DEC_PC, LD_PC, WE_RAM, OE_RAM, WE_MBR, IOE_MBR, OE_MBR, WE_IR, OE_IR, WE_MAR, OE_MAR, OP3_ALU, OP2_ALU, OP1_ALU, OP0_ALU, OE_ALU, OE_PC, WE_RA, OE_RA, WE_RB, OE_RB, WE_OR, OE_OR, WE_ADDR0, OE_ADDR0, WE_ADDR1, OE_ADDR1, CE_PC, WE_VR, OE_VR, DONE_SC, CLK_OFF
  RAM #(.addrWidth(15), .enables("line")) ram_1 (
    .addr(controlled_buffer_2_out), .we(WE_RAM), .clk(CLK), .din(EXT_DATA_BUS), .dout(ram_1_dout));
  assign EXT_DATA_BUS = and_2_out ? ram_1_dout : 8'bz;  // Controlled_Buffer controlled_buffer_4
  not not_2 (not_2_out, DEC_PC);
  ALU MyALU (
    .Reg_A(RA), .Reg_B(VR), .OE(OE_ALU), .OP_ALU(OP), .Dout(EXT_DATA_BUS), .ALU_Result(MyALU_alu_result));  // open: Carry_Out
  assign controlled_buffer_5_out = not_2_out ? 1'b1 : 1'bz;  // Controlled_Buffer controlled_buffer_5
  Hex_Digit_Display hex_digit_display_35 (.value(MyALU_alu_result[7:4]));  // open: dp
  Hex_Digit_Display hex_digit_display_36 (.value(MyALU_alu_result[3:0]));  // open: dp
  and and_2 (and_2_out, OE_RAM, EXT_ADDR_BUS[15]);
  Counter #(.max('hffff), .width(16)) ProgramCounter (
    .clr(RESET), .load(LD_PC), .up(controlled_buffer_5_out), .count(CE_PC), .clk(CLK), .D(INT_ADDR_BUS),
    .Q(PC));  // open: carry
  Counter StepCounter (
    .clr(RESET), .load(DONE_SC), .up(1'b1), .count(1'b1), .clk(CLK), .D({8{1'b0}}), .Q(SC));  // open: carry
  assign EXT_DATA_BUS = IOE_MBR ? MBR : 8'bz;  // Controlled_Buffer controlled_buffer_6
  assign INT_ADDR_BUS = OE_PC ? PC : 16'bz;  // Controlled_Buffer controlled_buffer_7
  MyRegister u_MBR (
    .OE(OE_MBR), .WE(WE_MBR), .Clock(CLK), .Reset(RESET), .Din(EXT_DATA_BUS), .Dout(EXT_DATA_BUS),
    .StoredData(MBR));
  MyRegister OutputRegister (
    .OE(OE_OR), .WE(WE_OR), .Clock(CLK), .Reset(RESET), .Din(EXT_DATA_BUS), .Dout(EXT_DATA_BUS),
    .StoredData(OR));
  Hex_Digit_Display hex_digit_display_37 (.value(SC[7:4]));  // open: dp
  Hex_Digit_Display hex_digit_display_38 (.value(MBR[7:4]));  // open: dp
  Hex_Digit_Display hex_digit_display_39 (.value(OR[7:4]));  // open: dp
  Hex_Digit_Display hex_digit_display_40 (.value(SC[3:0]));  // open: dp
  Hex_Digit_Display hex_digit_display_41 (.value(MBR[3:0]));  // open: dp
  Hex_Digit_Display hex_digit_display_42 (.value(OR[3:0]));  // open: dp

  // Other names for the same wires on the sheet: INT_DATA_BUS[7:0] = EXT_DATA_BUS

  // Notes on the sheet:
  //   Instruction Register
  //   Register A
  //   Register B
  //   Addr1Register
  //   External Address Bus
  //   Internal Address Bus
  //   Internal Data Bus
  //   External Data Bus
  //   contents of rom_1 (hex, n*v repeats v):
  //   3 aa 7 0 80 a 0 80
  //   MAR
  //   PROGRAM
  //   MEMORY
  //   BARIABELS
  //   Program Counter
  //   Step Counter
  //   MBR
  //   Output Register
endmodule

// c
module CU (
  input  opc4,
  input  opc3,
  input  opc2,
  input  opc1,
  input  opc0,
  input  sc3,
  input  sc2,
  input  sc1,
  input  sc0,
  output OE_PC,
  output CE_PC,
  output DEC_PC,
  output LD_PC,
  output WE_RAM,
  output OE_RAM,
  output WE_MBR,
  output IOE_MBR,
  output OE_MBR,
  output WE_IR,
  output OE_IR,
  output WE_MAR,
  output OE_MAR,
  output OP3_ALU,
  output OP2_ALU,
  output OP1_ALU,
  output OP0_ALU,
  output OE_ALU,
  output WE_RA,
  output OE_RA,
  output WE_RB,
  output OE_RB,
  output WE_OR,
  output OE_OR,
  output WE_ADDR0,
  output OE_ADDR0,
  output WE_ADDR1,
  output OE_ADDR1,
  output WE_VR,
  output OE_VR,
  output DONE_SC,
  output CLK_OFF
);

  wire and_1_out, and_2_out, and_3_out, and_4_out, and_5_out, and_6_out, and_7_out, and_8_out, and_9_out,
       and_10_out, and_11_out, and_12_out, and_13_out, and_14_out, and_15_out, and_16_out, and_17_out,
       and_18_out, and_19_out, and_20_out, and_21_out, and_22_out, and_23_out, and_24_out, and_25_out,
       and_26_out, and_27_out, and_28_out, and_29_out, and_30_out, and_31_out, and_32_out, and_33_out,
       and_34_out, and_35_out, and_36_out, and_37_out, and_38_out, and_39_out, and_40_out, and_41_out,
       and_42_out, and_43_out, and_44_out, and_45_out, and_46_out, and_47_out, and_48_out, and_49_out,
       and_50_out, and_51_out, and_52_out, and_53_out, and_54_out, and_55_out, and_56_out, and_57_out,
       and_58_out, and_59_out, and_60_out, and_61_out, and_62_out, and_63_out, and_64_out, and_65_out,
       and_66_out, and_67_out, and_68_out, and_69_out, and_70_out, and_71_out, and_72_out, and_73_out,
       and_74_out, and_75_out, and_76_out, and_77_out, and_78_out, and_79_out, and_80_out, and_81_out,
       and_82_out, and_83_out, and_84_out, and_86_out, and_87_out, and_88_out, and_89_out, and_90_out,
       and_91_out, and_92_out, and_93_out, and_94_out, and_95_out, and_96_out, and_97_out, and_98_out,
       and_99_out, and_100_out, and_101_out, and_102_out, and_103_out, and_104_out, and_105_out, and_106_out,
       and_107_out, and_108_out, and_109_out, and_110_out, and_111_out, and_112_out, and_113_out,
       and_114_out, and_115_out, and_116_out, and_117_out, and_118_out, and_119_out, and_120_out,
       and_121_out, and_122_out, and_123_out, and_124_out, and_125_out, and_126_out, and_127_out,
       and_128_out, and_129_out, and_130_out, and_131_out, and_132_out, and_133_out, and_134_out,
       and_135_out, and_136_out, and_137_out, and_138_out, and_139_out, and_140_out, and_141_out,
       and_142_out, and_143_out, and_144_out, and_145_out, and_146_out, and_147_out, and_148_out,
       and_149_out, and_150_out, and_151_out, and_152_out, and_153_out, and_154_out, and_155_out,
       and_156_out, and_157_out, and_158_out, and_159_out, and_160_out, and_161_out, and_162_out,
       and_163_out, and_164_out, and_165_out, and_166_out, and_167_out, and_168_out, and_169_out,
       and_170_out, and_171_out, and_172_out, and_173_out, and_174_out, and_175_out, and_176_out,
       and_177_out, and_178_out, and_179_out, and_180_out, and_181_out, and_182_out, and_183_out,
       and_184_out, and_185_out, and_186_out, and_187_out, and_188_out, and_189_out, and_190_out,
       and_191_out, and_192_out, and_193_out, and_194_out, and_195_out, and_196_out, and_197_out,
       and_198_out, and_199_out, and_200_out, and_201_out, and_202_out, and_203_out, and_204_out,
       and_205_out, and_206_out, and_207_out, and_208_out, and_209_out, and_211_out, and_212_out,
       and_213_out, and_214_out, and_215_out, and_216_out, and_217_out, and_218_out, and_219_out,
       and_220_out, and_221_out, and_222_out, and_223_out, and_224_out, and_225_out, and_226_out, not_1_out,
       not_2_out, not_3_out, not_4_out, not_5_out, not_6_out, not_7_out, not_8_out, not_9_out;

  not not_1 (not_1_out, opc4);
  not not_2 (not_2_out, opc3);
  not not_3 (not_3_out, opc2);
  not not_4 (not_4_out, opc1);
  not not_5 (not_5_out, opc0);
  not not_6 (not_6_out, sc3);
  not not_7 (not_7_out, sc2);
  not not_8 (not_8_out, sc1);
  not not_9 (not_9_out, sc0);
  and and_1 (and_1_out, not_6_out, not_7_out, not_8_out, not_9_out);
  and and_2 (and_2_out, opc3, not_4_out, not_6_out, not_7_out, sc1, sc0);
  and and_3 (and_3_out, opc3, not_3_out, not_4_out, not_5_out, not_6_out, sc2, sc1, not_9_out);
  and and_4 (and_4_out, opc4, opc0, not_6_out, not_7_out, sc1, sc0);
  and and_5 (and_5_out, opc4, opc0, not_6_out, sc2, sc1, not_9_out);
  and and_6 (and_6_out, opc4, opc1, not_6_out, not_7_out, sc1, sc0);
  and and_7 (and_7_out, opc4, opc1, not_6_out, sc2, sc1, not_9_out);
  and and_8 (and_8_out, not_2_out, opc1, opc0, not_6_out, not_7_out, sc1, sc0);
  and and_9 (and_9_out, opc2, not_6_out, not_7_out, sc1, sc0);
  and and_10 (and_10_out, opc4, opc2, not_6_out, sc2, sc1, not_9_out);
  and and_11 (and_11_out, not_2_out, opc2, opc0, not_6_out, sc2, sc1, not_9_out);
  and and_12 (and_12_out, not_2_out, opc2, opc1, not_6_out, sc2, sc1, not_9_out);
  and and_13 (and_13_out, not_6_out, not_7_out, not_8_out, sc0);
  and and_14 (and_14_out, opc3, not_4_out, not_6_out, sc2, not_8_out, not_9_out);
  and and_15 (and_15_out, opc3, not_3_out, not_4_out, not_5_out, not_6_out, sc2, sc1, sc0);
  and and_16 (and_16_out, opc4, opc0, not_6_out, sc2, not_8_out, not_9_out);
  and and_17 (and_17_out, opc4, opc0, not_6_out, sc2, sc1, sc0);
  and and_18 (and_18_out, opc4, opc1, not_6_out, sc2, not_8_out, not_9_out);
  and and_19 (and_19_out, opc4, opc1, not_6_out, sc2, sc1, sc0);
  and and_20 (and_20_out, not_2_out, opc1, opc0, not_6_out, sc2, not_8_out, not_9_out);
  and and_21 (and_21_out, opc2, not_6_out, sc2, not_8_out, not_9_out);
  and and_22 (and_22_out, opc4, opc2, not_6_out, sc2, sc1, sc0);
  and and_23 (and_23_out, not_2_out, opc2, opc0, not_6_out, sc2, sc1, sc0);
  and and_24 (and_24_out, not_2_out, opc2, opc1, not_6_out, sc2, sc1, sc0);
  and and_25 (and_25_out, not_1_out, not_2_out, opc2, opc1, opc0, sc3, not_7_out, sc1, not_9_out);
  and and_26 (and_26_out, opc3, not_3_out, not_4_out, not_5_out, sc3, not_7_out, sc1, not_9_out);
  and and_27 (and_27_out, opc4, opc2, opc1, sc3, sc2, not_8_out, sc0);
  and and_28 (and_28_out, not_6_out, not_7_out, not_8_out, sc0);
  and and_29 (and_29_out, opc3, not_4_out, not_6_out, sc2, not_8_out, not_9_out);
  and and_30 (and_30_out, opc3, not_3_out, not_4_out, not_5_out, not_6_out, sc2, sc1, sc0);
  and and_31 (and_31_out, opc4, opc0, not_6_out, sc2, not_8_out, not_9_out);
  and and_32 (and_32_out, opc4, opc0, not_6_out, sc2, sc1, sc0);
  and and_33 (and_33_out, opc4, opc1, not_6_out, sc2, not_8_out, not_9_out);
  and and_34 (and_34_out, opc4, opc1, not_6_out, sc2, sc1, sc0);
  and and_35 (and_35_out, opc4, not_3_out, opc1, sc3, not_7_out, sc1, not_9_out);
  and and_36 (and_36_out, not_2_out, opc1, opc0, not_6_out, sc2, not_8_out, not_9_out);
  and and_37 (and_37_out, opc2, not_6_out, sc2, not_8_out, not_9_out);
  and and_38 (and_38_out, opc4, opc2, not_6_out, sc2, sc1, sc0);
  and and_39 (and_39_out, opc4, opc2, not_4_out, sc3, not_7_out, sc1, not_9_out);
  and and_40 (and_40_out, not_2_out, opc2, opc0, not_6_out, sc2, sc1, sc0);
  and and_41 (and_41_out, not_2_out, opc2, not_4_out, opc0, sc3, not_7_out, sc1, not_9_out);
  and and_42 (and_42_out, not_2_out, opc2, opc1, not_6_out, sc2, sc1, sc0);
  and and_43 (and_43_out, not_1_out, not_2_out, opc2, opc1, not_5_out, sc3, not_7_out, sc1, not_9_out);
  and and_44 (and_44_out, opc4, not_3_out, opc0, sc3, not_7_out, sc1, not_9_out);
  and and_45 (and_45_out, not_6_out, not_7_out, not_8_out, sc0);
  and and_46 (and_46_out, opc3, not_4_out, not_6_out, sc2, not_8_out, not_9_out);
  and and_47 (and_47_out, opc3, not_3_out, not_4_out, not_5_out, not_6_out, sc2, sc1, sc0);
  and and_48 (and_48_out, opc3, not_3_out, not_4_out, not_5_out, not_7_out, not_8_out, sc0);
  and and_49 (and_49_out, opc4, opc0, not_6_out, sc2, not_8_out, not_9_out);
  and and_50 (and_50_out, opc4, opc0, not_6_out, sc2, sc1, sc0);
  and and_51 (and_51_out, opc4, opc1, not_6_out, sc2, not_8_out, not_9_out);
  and and_52 (and_52_out, opc4, opc1, not_6_out, sc2, sc1, sc0);
  and and_53 (and_53_out, opc4, not_3_out, opc1, sc3, not_7_out, sc1, not_9_out);
  and and_54 (and_54_out, not_2_out, opc1, opc0, not_6_out, sc2, not_8_out, not_9_out);
  and and_55 (and_55_out, opc2, not_6_out, sc2, not_8_out, not_9_out);
  and and_56 (and_56_out, opc4, opc2, not_6_out, sc2, sc1, sc0);
  and and_57 (and_57_out, opc4, opc2, not_4_out, sc3, not_7_out, sc1, not_9_out);
  and and_58 (and_58_out, not_2_out, opc2, opc0, not_6_out, sc2, sc1, sc0);
  and and_59 (and_59_out, not_2_out, opc2, not_4_out, opc0, sc3, not_7_out, sc1, not_9_out);
  and and_60 (and_60_out, not_2_out, opc2, opc1, not_6_out, sc2, sc1, sc0);
  and and_61 (and_61_out, not_1_out, not_2_out, opc2, opc1, not_5_out, sc3, not_7_out, sc1, not_9_out);
  and and_62 (and_62_out, opc4, opc2, opc1, sc2, not_8_out, not_9_out);
  and and_63 (and_63_out, not_1_out, not_2_out, opc2, opc1, opc0, not_7_out, not_8_out, sc0);
  and and_64 (and_64_out, opc4, not_3_out, opc0, sc3, not_7_out, sc1, not_9_out);
  and and_65 (and_65_out, not_6_out, not_7_out, sc1, not_9_out);
  and and_66 (and_66_out, opc3, not_4_out, not_6_out, sc2, not_8_out, sc0);
  and and_67 (and_67_out, opc3, not_3_out, not_4_out, not_5_out, sc3, not_7_out, not_8_out, not_9_out);
  and and_68 (and_68_out, opc4, opc0, not_6_out, sc2, not_8_out, sc0);
  and and_69 (and_69_out, opc4, opc0, sc3, not_7_out, not_8_out, not_9_out);
  and and_70 (and_70_out, opc4, opc0, sc3, not_7_out, sc1, sc0);
  and and_71 (and_71_out, opc4, opc1, not_6_out, sc2, not_8_out, sc0);
  and and_72 (and_72_out, opc4, opc1, sc3, not_7_out, not_8_out, not_9_out);
  and and_73 (and_73_out, opc4, opc1, sc3, not_7_out, sc1, sc0);
  and and_74 (and_74_out, not_2_out, opc1, opc0, not_6_out, sc2, not_8_out, sc0);
  and and_75 (and_75_out, opc2, not_6_out, sc2, not_8_out, sc0);
  and and_76 (and_76_out, opc4, opc2, sc3, not_7_out, not_8_out, not_9_out);
  and and_77 (and_77_out, opc4, opc2, sc3, not_7_out, sc1, sc0);
  and and_78 (and_78_out, not_2_out, opc2, opc0, sc3, not_7_out, not_8_out, not_9_out);
  and and_79 (and_79_out, not_2_out, opc2, not_4_out, opc0, sc3, not_7_out, sc1, sc0);
  and and_80 (and_80_out, not_2_out, opc2, opc1, sc3, not_7_out, not_8_out, not_9_out);
  and and_81 (and_81_out, not_2_out, opc2, opc1, not_5_out, sc3, not_7_out, sc1, sc0);
  and and_82 (and_82_out, not_1_out, not_2_out, opc2, opc1, opc0, sc3, not_7_out, sc1, not_9_out);
  and and_83 (and_83_out, opc3, not_3_out, not_4_out, not_5_out, sc3, not_7_out, sc1, not_9_out);
  and and_84 (and_84_out, opc4, opc2, opc1, sc3, sc2, not_8_out, sc0);
  and and_85 (WE_IR, not_6_out, not_7_out, sc1, not_9_out);
  and and_86 (and_86_out, not_6_out, not_7_out, not_8_out, not_9_out);
  and and_87 (and_87_out, opc3, not_4_out, not_6_out, not_7_out, sc1, sc0);
  and and_88 (and_88_out, opc3, not_3_out, not_4_out, not_5_out, not_6_out, sc2, sc1, not_9_out);
  and and_89 (and_89_out, opc3, not_3_out, not_4_out, not_5_out, sc3, not_7_out, not_8_out, sc0);
  and and_90 (and_90_out, opc4, opc0, not_6_out, not_7_out, sc1, sc0);
  and and_91 (and_91_out, opc4, opc0, not_6_out, sc2, sc1, not_9_out);
  and and_92 (and_92_out, opc4, opc0, sc3, not_7_out, not_8_out, sc0);
  and and_93 (and_93_out, opc4, opc1, not_6_out, not_7_out, sc1, sc0);
  and and_94 (and_94_out, opc4, opc1, not_6_out, sc2, sc1, not_9_out);
  and and_95 (and_95_out, opc4, opc1, sc3, not_7_out, not_8_out, sc0);
  and and_96 (and_96_out, not_2_out, opc1, opc0, not_6_out, not_7_out, sc1, sc0);
  and and_97 (and_97_out, opc2, not_6_out, not_7_out, sc1, sc0);
  and and_98 (and_98_out, opc4, opc2, not_6_out, sc2, sc1, not_9_out);
  and and_99 (and_99_out, opc4, opc2, sc3, not_7_out, not_8_out, sc0);
  and and_100 (and_100_out, not_2_out, opc2, opc0, not_6_out, sc2, sc1, not_9_out);
  and and_101 (and_101_out, not_2_out, opc2, opc0, sc3, not_7_out, not_8_out, sc0);
  and and_102 (and_102_out, not_2_out, opc2, opc1, not_6_out, sc2, sc1, not_9_out);
  and and_103 (and_103_out, not_2_out, opc2, opc1, sc3, not_7_out, not_8_out, sc0);
  and and_104 (and_104_out, not_6_out, not_7_out, not_8_out, sc0);
  and and_105 (and_105_out, opc3, not_4_out, not_6_out, sc2, not_8_out, not_9_out);
  and and_106 (and_106_out, opc3, not_3_out, not_4_out, not_5_out, not_6_out, sc2, sc1, sc0);
  and and_107 (and_107_out, opc3, not_3_out, not_4_out, not_5_out, sc3, not_7_out, sc1, not_9_out);
  and and_108 (and_108_out, opc4, opc0, not_6_out, sc2, not_8_out, not_9_out);
  and and_109 (and_109_out, opc4, opc0, not_6_out, sc2, sc1, sc0);
  and and_110 (and_110_out, opc4, opc1, not_6_out, sc2, not_8_out, not_9_out);
  and and_111 (and_111_out, opc4, opc1, not_6_out, sc2, sc1, sc0);
  and and_112 (and_112_out, opc4, not_3_out, opc1, sc3, not_7_out, sc1, not_9_out);
  and and_113 (and_113_out, not_2_out, opc1, opc0, not_6_out, sc2, not_8_out, not_9_out);
  and and_114 (and_114_out, opc2, not_6_out, sc2, not_8_out, not_9_out);
  and and_115 (and_115_out, opc4, opc2, not_6_out, sc2, sc1, sc0);
  and and_116 (and_116_out, opc4, opc2, not_4_out, sc3, not_7_out, sc1, not_9_out);
  and and_117 (and_117_out, not_2_out, opc2, opc0, not_6_out, sc2, sc1, sc0);
  and and_118 (and_118_out, not_2_out, opc2, opc1, not_6_out, sc2, sc1, sc0);
  and and_119 (and_119_out, not_1_out, not_2_out, opc2, opc1, sc3, not_7_out, sc1, not_9_out);
  and and_120 (and_120_out, opc4, opc2, opc1, sc3, sc2, not_8_out, sc0);
  and and_121 (and_121_out, opc4, not_3_out, opc0, sc3, not_7_out, sc1, not_9_out);
  and and_122 (and_122_out, not_2_out, opc2, not_4_out, opc0, sc3, not_7_out, sc1, not_9_out);
  and and_123 (and_123_out, opc4, not_3_out, not_4_out, not_5_out, not_6_out, not_7_out, sc1, sc0);
  and and_124 (and_124_out, opc3, opc2, opc0, not_6_out, sc2, sc1, not_9_out);
  and and_125 (and_125_out, opc3, opc2, opc1, not_6_out, sc2, sc1, not_9_out);
  and and_126 (and_126_out, opc4, not_3_out, opc1, opc0, sc3, sc2, not_8_out, not_9_out);
  and and_127 (and_127_out, opc4, opc2, not_4_out, sc3, sc2, not_8_out, not_9_out);
  and and_128 (and_128_out, opc3, not_3_out, opc1, not_6_out, not_7_out, sc1, sc0);
  and and_129 (and_129_out, opc4, not_3_out, not_4_out, not_5_out, not_6_out, not_7_out, sc1, sc0);
  and and_130 (and_130_out, opc3, opc2, opc1, opc0, not_6_out, sc2, sc1, not_9_out);
  and and_131 (and_131_out, opc4, opc2, opc0, sc3, sc2, not_8_out, not_9_out);
  and and_132 (and_132_out, opc4, opc2, opc1, sc3, sc2, not_8_out, not_9_out);
  and and_133 (and_133_out, opc3, not_3_out, opc1, opc0, not_6_out, not_7_out, sc1, sc0);
  and and_134 (and_134_out, opc4, not_3_out, not_4_out, not_5_out, not_6_out, not_7_out, sc1, sc0);
  and and_135 (and_135_out, opc3, opc2, not_5_out, not_6_out, sc2, sc1, not_9_out);
  and and_136 (and_136_out, opc4, not_3_out, opc1, not_5_out, sc3, sc2, not_8_out, not_9_out);
  and and_137 (and_137_out, opc4, opc2, not_4_out, not_5_out, sc3, sc2, not_8_out, not_9_out);
  and and_138 (and_138_out, opc4, opc2, opc1, opc0, sc3, sc2, not_8_out, not_9_out);
  and and_139 (and_139_out, opc3, not_3_out, opc1, not_6_out, not_7_out, sc1, sc0);
  and and_140 (and_140_out, opc4, not_3_out, not_4_out, not_5_out, not_6_out, not_7_out, sc1, sc0);
  and and_141 (and_141_out, opc3, opc2, not_6_out, sc2, sc1, not_9_out);
  and and_142 (and_142_out, opc4, opc1, sc3, sc2, not_8_out, not_9_out);
  and and_143 (and_143_out, opc4, opc2, sc3, sc2, not_8_out, not_9_out);
  and and_144 (and_144_out, opc3, not_4_out, opc0, not_6_out, sc2, sc1, not_9_out);
  and and_145 (and_145_out, opc4, opc0, sc3, sc2, not_8_out, not_9_out);
  and and_146 (and_146_out, not_1_out, not_2_out, not_3_out, opc1, not_5_out, not_6_out, not_7_out, sc1, sc0);
  and and_147 (and_147_out, opc3, not_3_out, opc1, not_6_out, sc2, not_8_out, not_9_out);
  and and_148 (and_148_out, opc4, not_3_out, not_4_out, not_5_out, not_6_out, sc2, not_8_out, not_9_out);
  and and_149 (and_149_out, opc3, opc2, not_6_out, sc2, sc1, sc0);
  and and_150 (and_150_out, opc4, opc2, opc1, sc3, not_7_out, sc1, sc0);
  and and_151 (and_151_out, opc4, not_3_out, opc1, sc3, sc2, not_8_out, sc0);
  and and_152 (and_152_out, opc4, opc2, not_4_out, sc3, sc2, not_8_out, sc0);
  and and_153 (and_153_out, opc4, opc2, opc1, sc3, sc2, sc1, not_9_out);
  and and_154 (and_154_out, not_1_out, not_2_out, not_3_out, opc1, opc0, not_6_out, sc2, not_8_out, sc0);
  and and_155 (and_155_out, opc3, not_4_out, opc0, not_6_out, sc2, sc1, sc0);
  and and_156 (and_156_out, not_1_out, not_2_out, opc2, not_4_out, opc0, sc3, not_7_out, sc1, sc0);
  and and_157 (and_157_out, opc4, not_3_out, opc0, sc3, sc2, not_8_out, sc0);
  and and_158 (and_158_out, not_1_out, not_2_out, not_3_out, not_4_out, opc0, not_6_out, not_7_out, sc1, sc0);
  and and_159 (and_159_out, not_1_out, not_2_out, opc2, opc1, opc0, sc3, not_7_out, not_8_out, sc0);
  and and_160 (and_160_out, opc4, opc2, opc1, sc3, not_7_out, sc1, not_9_out);
  and and_161 (and_161_out, not_1_out, not_2_out, not_3_out, not_4_out, opc0, not_6_out, not_7_out, sc1, sc0);
  and and_162 (and_162_out, not_1_out, not_2_out, opc2, not_4_out, not_5_out, not_6_out, sc2, not_8_out, sc0);
  and and_163 (and_163_out, not_1_out, not_2_out, opc2, opc1, not_5_out, sc3, not_7_out, sc1, sc0);
  and and_164 (and_164_out, not_1_out, not_2_out, not_3_out, opc1, not_5_out, not_6_out, not_7_out, sc1, sc0);
  and and_165 (and_165_out, opc3, not_3_out, not_4_out, not_5_out, sc3, not_7_out, not_8_out, sc0);
  and and_166 (and_166_out, opc3, not_3_out, opc1, not_6_out, not_7_out, sc1, sc0);
  and and_167 (and_167_out, opc4, not_3_out, not_4_out, not_5_out, not_6_out, not_7_out, sc1, sc0);
  and and_168 (and_168_out, opc3, opc2, not_6_out, sc2, sc1, not_9_out);
  and and_169 (and_169_out, opc4, not_3_out, opc1, sc3, sc2, not_8_out, not_9_out);
  and and_170 (and_170_out, opc4, opc2, not_4_out, sc3, sc2, not_8_out, not_9_out);
  and and_171 (and_171_out, opc3, not_4_out, opc0, not_6_out, sc2, sc1, not_9_out);
  and and_172 (and_172_out, opc4, not_3_out, opc0, sc3, sc2, not_8_out, not_9_out);
  and and_173 (and_173_out, opc3, not_3_out, opc1, not_6_out, sc2, not_8_out, not_9_out);
  and and_174 (and_174_out, opc4, not_3_out, not_4_out, not_5_out, not_6_out, sc2, not_8_out, not_9_out);
  and and_175 (and_175_out, opc3, opc2, not_6_out, sc2, sc1, sc0);
  and and_176 (and_176_out, opc4, not_3_out, opc1, sc3, sc2, not_8_out, sc0);
  and and_177 (and_177_out, opc4, opc2, not_4_out, sc3, sc2, not_8_out, sc0);
  and and_178 (and_178_out, opc3, not_4_out, opc0, not_6_out, sc2, sc1, sc0);
  and and_179 (and_179_out, opc4, not_3_out, opc0, sc3, sc2, not_8_out, sc0);
  and and_180 (and_180_out, not_2_out, opc2, opc1, not_6_out, sc2, not_8_out, sc0);
  and and_181 (and_181_out, opc3, not_3_out, not_4_out, not_5_out, not_6_out, sc2, not_8_out, sc0);
  and and_182 (and_182_out, opc4, opc1, not_6_out, sc2, not_8_out, sc0);
  and and_183 (and_183_out, opc4, opc2, not_6_out, sc2, not_8_out, sc0);
  and and_184 (and_184_out, not_2_out, opc2, opc0, not_6_out, sc2, not_8_out, sc0);
  and and_185 (and_185_out, opc4, opc0, not_6_out, sc2, not_8_out, sc0);
  and and_186 (and_186_out, not_2_out, opc2, opc1, sc3, not_7_out, not_8_out, sc0);
  and and_187 (and_187_out, opc3, not_3_out, not_4_out, not_5_out, sc3, not_7_out, not_8_out, sc0);
  and and_188 (and_188_out, opc4, opc1, sc3, not_7_out, not_8_out, sc0);
  and and_189 (and_189_out, opc4, opc2, sc3, not_7_out, not_8_out, sc0);
  and and_190 (and_190_out, not_2_out, opc2, opc0, sc3, not_7_out, not_8_out, sc0);
  and and_191 (and_191_out, opc4, opc0, sc3, not_7_out, not_8_out, sc0);
  and and_192 (and_192_out, not_2_out, opc2, opc1, sc3, not_7_out, not_8_out, not_9_out);
  and and_193 (and_193_out, opc3, not_3_out, not_4_out, not_5_out, sc3, not_7_out, not_8_out, not_9_out);
  and and_194 (and_194_out, opc4, opc1, sc3, not_7_out, not_8_out, not_9_out);
  and and_195 (and_195_out, opc4, opc2, sc3, not_7_out, not_8_out, not_9_out);
  and and_196 (and_196_out, not_2_out, opc2, opc0, sc3, not_7_out, not_8_out, not_9_out);
  and and_197 (and_197_out, opc4, opc0, sc3, not_7_out, not_8_out, not_9_out);
  and and_198 (and_198_out, not_2_out, opc2, opc1, sc3, not_7_out, not_8_out, sc0);
  and and_199 (and_199_out, opc3, not_3_out, not_4_out, not_5_out, sc3, not_7_out, not_8_out, sc0);
  and and_200 (and_200_out, opc4, opc1, sc3, not_7_out, not_8_out, sc0);
  and and_201 (and_201_out, opc4, opc2, sc3, not_7_out, not_8_out, sc0);
  and and_202 (and_202_out, not_2_out, opc2, opc0, sc3, not_7_out, not_8_out, sc0);
  and and_203 (and_203_out, opc4, opc0, sc3, not_7_out, not_8_out, sc0);
  and and_204 (and_204_out, opc3, not_4_out, opc0, not_6_out, sc2, not_8_out, sc0);
  and and_205 (and_205_out, opc3, opc2, not_6_out, sc2, not_8_out, sc0);
  and and_206 (and_206_out, opc4, opc2, opc1, sc3, not_7_out, sc1, not_9_out);
  and and_207 (and_207_out, opc4, not_3_out, opc1, sc3, not_7_out, sc1, sc0);
  and and_208 (and_208_out, opc4, opc2, not_4_out, sc3, not_7_out, sc1, sc0);
  and and_209 (and_209_out, opc4, not_3_out, opc0, sc3, not_7_out, sc1, sc0);
  and and_210 (OE_VR, opc4, opc2, opc1, sc3, sc2, sc1, not_9_out);
  and and_211 (and_211_out, not_1_out, not_2_out, not_3_out, not_5_out, not_6_out, sc2, not_8_out, not_9_out);
  and and_212 (and_212_out, opc3, not_3_out, opc1, not_6_out, sc2, not_8_out, sc0);
  and and_213 (and_213_out, opc4, not_3_out, not_4_out, not_5_out, not_6_out, sc2, not_8_out, sc0);
  and and_214 (and_214_out, not_1_out, not_2_out, opc2, not_4_out, not_5_out, not_6_out, sc2, sc1, not_9_out);
  and and_215 (and_215_out, opc3, opc2, sc3, not_7_out, not_8_out, not_9_out);
  and and_216 (and_216_out, opc3, not_3_out, not_4_out, not_5_out, sc3, not_7_out, sc1, sc0);
  and and_217 (and_217_out, not_1_out, not_2_out, opc2, opc1, not_5_out, sc3, sc2, not_8_out, not_9_out);
  and and_218 (and_218_out, opc4, not_3_out, opc1, sc3, sc2, sc1, not_9_out);
  and and_219 (and_219_out, opc4, opc2, not_4_out, sc3, sc2, sc1, not_9_out);
  and and_220 (and_220_out, opc4, opc2, opc1, sc3, sc2, sc1, sc0);
  and and_221 (and_221_out, not_1_out, not_2_out, not_3_out, not_4_out, not_6_out, sc2, not_8_out, not_9_out);
  and and_222 (and_222_out, not_1_out, not_2_out, not_3_out, opc1, opc0, not_6_out, sc2, sc1, not_9_out);
  and and_223 (and_223_out, opc3, not_4_out, opc0, sc3, not_7_out, not_8_out, not_9_out);
  and and_224 (and_224_out, not_1_out, not_2_out, opc2, opc1, opc0, sc3, not_7_out, sc1, sc0);
  and and_225 (and_225_out, not_1_out, not_2_out, opc2, not_4_out, opc0, sc3, sc2, not_8_out, not_9_out);
  and and_226 (and_226_out, opc4, not_3_out, opc0, sc3, sc2, sc1, not_9_out);
  and and_227 (CLK_OFF, not_1_out, not_2_out, not_3_out, not_4_out, not_5_out, not_6_out, not_7_out, sc1, sc0);
  or or_1 (WE_RAM, and_25_out, and_26_out, and_27_out);
  or or_2 (OE_MBR, and_82_out, and_83_out, and_84_out);
  or or_3 (OP2_ALU, and_123_out, and_124_out, and_125_out, and_126_out, and_127_out);
  or or_4 (OP1_ALU, and_128_out, and_129_out, and_130_out, and_131_out, and_132_out);
  or or_5 (OE_RA, and_158_out, and_159_out, and_160_out);
  or or_6 (WE_RB, and_161_out, and_162_out, and_163_out);
  or or_7 (OE_RB, and_164_out, and_165_out);
  or or_8 (OE_PC, and_1_out, and_2_out, and_3_out, and_4_out, and_5_out, and_6_out, and_7_out, and_8_out, and_9_out, and_10_out, and_11_out, and_12_out);
  or or_9 (CE_PC, and_13_out, and_14_out, and_15_out, and_16_out, and_17_out, and_18_out, and_19_out, and_20_out, and_21_out, and_22_out, and_23_out, and_24_out);
  or or_10 (OE_RAM, and_28_out, and_29_out, and_30_out, and_31_out, and_32_out, and_33_out, and_34_out, and_35_out, and_36_out, and_37_out, and_38_out, and_39_out, and_40_out, and_41_out, and_42_out, and_43_out, and_44_out);
  or or_11 (WE_MBR, and_45_out, and_46_out, and_47_out, and_48_out, and_49_out, and_50_out, and_51_out, and_52_out, and_53_out, and_54_out, and_55_out, and_56_out, and_57_out, and_58_out, and_59_out, and_60_out, and_61_out, and_62_out, and_63_out, and_64_out);
  or or_12 (IOE_MBR, and_65_out, and_66_out, and_67_out, and_68_out, and_69_out, and_70_out, and_71_out, and_72_out, and_73_out, and_74_out, and_75_out, and_76_out, and_77_out, and_78_out, and_79_out, and_80_out, and_81_out);
  or or_13 (WE_MAR, and_86_out, and_87_out, and_88_out, and_89_out, and_90_out, and_91_out, and_92_out, and_93_out, and_94_out, and_95_out, and_96_out, and_97_out, and_98_out, and_99_out, and_100_out, and_101_out, and_102_out, and_103_out);
  or or_14 (OE_MAR, and_104_out, and_105_out, and_106_out, and_107_out, and_108_out, and_109_out, and_110_out, and_111_out, and_112_out, and_113_out, and_114_out, and_115_out, and_116_out, and_117_out, and_118_out, and_119_out, and_120_out, and_121_out, and_122_out);
  or or_15 (OP0_ALU, and_133_out, and_134_out, and_135_out, and_136_out, and_137_out, and_138_out);
  or or_16 (OE_ALU, and_139_out, and_140_out, and_141_out, and_142_out, and_143_out, and_144_out, and_145_out);
  or or_17 (WE_RA, and_146_out, and_147_out, and_148_out, and_149_out, and_150_out, and_151_out, and_152_out, and_153_out, and_154_out, and_155_out, and_156_out, and_157_out);
  or or_18 (WE_OR, and_166_out, and_167_out, and_168_out, and_169_out, and_170_out, and_171_out, and_172_out);
  or or_19 (OE_OR, and_173_out, and_174_out, and_175_out, and_176_out, and_177_out, and_178_out, and_179_out);
  or or_20 (WE_ADDR0, and_180_out, and_181_out, and_182_out, and_183_out, and_184_out, and_185_out);
  or or_21 (OE_ADDR0, and_186_out, and_187_out, and_188_out, and_189_out, and_190_out, and_191_out);
  or or_22 (WE_ADDR1, and_192_out, and_193_out, and_194_out, and_195_out, and_196_out, and_197_out);
  or or_23 (OE_ADDR1, and_198_out, and_199_out, and_200_out, and_201_out, and_202_out, and_203_out);
  or or_24 (WE_VR, and_204_out, and_205_out, and_206_out, and_207_out, and_208_out, and_209_out);
  or or_25 (DONE_SC, and_211_out, and_212_out, and_213_out, and_214_out, and_215_out, and_216_out, and_217_out, and_218_out, and_219_out, and_220_out, and_221_out, and_222_out, and_223_out, and_224_out, and_225_out, and_226_out);

  assign DEC_PC = 1'b0;
  assign LD_PC = 1'b0;
  assign OE_IR = 1'b0;
  assign OP3_ALU = 1'b0;
endmodule

module MemoryCell (
  input  Clock,
  input  WE,
  input  Din,
  input  OE,
  input  Reset,
  output Dout,
  output StoredData
);

  wire and_1_out, and_2_out, not_1_out, or_1_out;

  not not_1 (not_1_out, WE);
  and and_1 (and_1_out, StoredData, not_1_out);
  and and_2 (and_2_out, WE, Din);
  or or_1 (or_1_out, and_1_out, and_2_out);
  D_Flip_Flop d_ff_1 (.D(or_1_out), .clk(Clock), .Q(StoredData), .reset(Reset));  // open: Qn, preset
  assign Dout = OE ? StoredData : 1'bz;  // Controlled_Buffer controlled_buffer_1
endmodule

module MyRegister (
  input  Reset,
  input  OE,
  input  [7:0] Din,
  input  WE,
  input  Clock,
  output [7:0] Dout,
  output [7:0] StoredData
);

  MemoryCell R0 (
    .WE(WE), .Din(Din[0]), .OE(OE), .Reset(Reset), .Clock(Clock), .Dout(Dout[0]), .StoredData(StoredData[0]));
  MemoryCell R1 (
    .WE(WE), .Din(Din[1]), .OE(OE), .Reset(Reset), .Clock(Clock), .Dout(Dout[1]), .StoredData(StoredData[1]));
  MemoryCell R2 (
    .WE(WE), .Din(Din[2]), .OE(OE), .Clock(Clock), .Dout(Dout[2]), .StoredData(StoredData[2]));  // open: Reset
  MemoryCell memorycell_1 (
    .WE(WE), .Din(Din[3]), .OE(OE), .Reset(Reset), .Clock(Clock), .Dout(Dout[3]), .StoredData(StoredData[3]));
  MemoryCell R (
    .WE(WE), .Din(Din[4]), .OE(OE), .Reset(Reset), .Clock(Clock), .Dout(Dout[4]), .StoredData(StoredData[4]));
  MemoryCell R5 (
    .WE(WE), .Din(Din[5]), .OE(OE), .Reset(Reset), .Clock(Clock), .Dout(Dout[5]), .StoredData(StoredData[5]));
  MemoryCell R6 (
    .WE(WE), .Din(Din[6]), .OE(OE), .Reset(Reset), .Clock(Clock), .Dout(Dout[6]), .StoredData(StoredData[6]));
  MemoryCell R7 (
    .WE(WE), .Din(Din[7]), .OE(OE), .Reset(Reset), .Clock(Clock), .Dout(Dout[7]), .StoredData(StoredData[7]));
endmodule

module ALUs (
  input  [7:0] Reg_A,
  input  [7:0] Reg_B,
  input  OE,
  output [7:0] Dout,
  output [7:0] ALU_Result,
  output Carry_Out
);

  Adder adder_1 (.a(Reg_A), .b(Reg_B), .out(ALU_Result), .cout(Carry_Out));  // open: cin
  assign Dout = OE ? ALU_Result : 8'bz;  // Controlled_Buffer controlled_buffer_1

  // Notes on the sheet:
  //   ALU (8Bit)
endmodule

module DecimalDecoder (
  input  [7:0] Din,
  output [31:0] Dout
);

  ROM #(.dataWidth(32)) rom_1 (
    .addr(Din),
    .data({Dout[31:28], Dout[15:12], Dout[27:24], Dout[11:8], Dout[23:20], Dout[7:4], Dout[19:16], Dout[3:0]}));

  // Notes on the sheet:
  //   contents of rom_1 (hex, n*v repeats v):
  //   e7 21 cb 6b 2d 6e ee 23 ef 2f 21e7 2121 21cb 216b 212d 216e 21ee 2123 21ef 212f cbe7 cb21 cbcb cb6b
  //   cb2d cb6e cbee cb23 cbef cb2f 6be7 6b21 6bcb 6b6b 6b2d 6b6e 6bee 6b23 6bef 6b2f 2de7 2d21 2dcb 2d6b
  //   2d2d 2d6e 2dee 2d23 2def 2d2f 6ee7 6e21 6ecb 6e6b 6e2d 6e6e 6eee 6e23 6eef 6e2f eee7 ee21 eecb ee6b
  //   ee2d ee6e eeee ee23 eeef ee2f 23e7 2321 23cb 236b 232d 236e 23ee 2323 23ef 232f efe7 ef21 efcb ef6b
  //   ef2d ef6e efee ef23 efef ef2f 2fe7 2f21 2fcb 2f6b 2f2d 2f6e 2fee 2f23 2fef 2f2f 21e7e7 21e721 21e7cb
  //   21e76b 21e72d 21e76e 21e7ee 21e723 21e7ef 21e72f 2121e7 212121 2121cb 21216b 21212d 21216e 2121ee
  //   212123 2121ef 21212f 21cbe7 21cb21 21cbcb 21cb6b 21cb2d 21cb6e 21cbee 21cb23 21cbef 21cb2f 216be7
  //   216b21 216bcb 216b6b 216b2d 216b6e 216bee 216b23 216bef 216b2f 212de7 212d21 212dcb 212d6b 212d2d
  //   212d6e 212dee 212d23 212def 212d2f 216ee7 216e21 216ecb 216e6b 216e2d 216e6e 216eee 216e23 216eef
  //   216e2f 21eee7 21ee21 21eecb 21ee6b 21ee2d 21ee6e 21eeee 21ee23 21eeef 21ee2f 2123e7 212321 2123cb
  //   21236b 21232d 21236e 2123ee 212323 2123ef 21232f 21efe7 21ef21 21efcb 21ef6b 21ef2d 21ef6e 21efee
  //   21ef23 21efef 21ef2f 212fe7 212f21 212fcb 212f6b 212f2d 212f6e 212fee 212f23 212fef 212f2f cbe7e7
  //   cbe721 cbe7cb cbe76b cbe72d cbe76e cbe7ee cbe723 cbe7ef cbe72f cb21e7 cb2121 cb21cb cb216b cb212d
  //   cb216e cb21ee cb2123 cb21ef cb212f cbcbe7 cbcb21 cbcbcb cbcb6b cbcb2d cbcb6e cbcbee cbcb23 cbcbef
  //   cbcb2f cb6be7 cb6b21 cb6bcb cb6b6b cb6b2d cb6b6e cb6bee cb6b23 cb6bef cb6b2f cb2de7 cb2d21 cb2dcb
  //   cb2d6b cb2d2d cb2d6e cb2dee cb2d23 cb2def cb2d2f cb6ee7 cb6e21 cb6ecb cb6e6b cb6e2d cb6e6e
endmodule

module Register16Bit (
  input  [15:0] Din,
  input  OE,
  input  WE,
  input  Clk,
  input  Reset,
  output [15:0] Dout,
  output [15:0] SD
);

  MyRegister myregister_1 (
    .OE(OE), .WE(WE), .Clock(Clk), .Reset(Reset), .Din(Din[7:0]), .Dout(Dout[7:0]), .StoredData(SD[7:0]));
  MyRegister myregister_2 (
    .OE(OE), .WE(WE), .Clock(Clk), .Reset(Reset), .Din(Din[15:8]), .Dout(Dout[15:8]), .StoredData(SD[15:8]));
endmodule

module ALU (
  input  [7:0] Reg_A,
  input  [7:0] Reg_B,
  input  OE,
  input  [2:0] OP_ALU,
  output Carry_Out,
  output [7:0] Dout,
  output [7:0] ALU_Result
);

  wire op_decoder_1_o0, op_decoder_1_o1, op_decoder_1_o2, op_decoder_1_o3, op_decoder_1_o4, op_decoder_1_o5,
       op_decoder_1_o6, op_decoder_1_o7;
  wire [7:0] adder_1_out, adder_2_out, and8bit_1_res, not_1_out, or8bit_1_res, subtractor_1_out,
       subtractor_2_out, xor8bit_1_res;

  Adder adder_1 (.a(Reg_A), .b(Reg_B), .out(adder_1_out), .cout(Carry_Out));  // open: cin
  Subtractor subtractor_1 (.a(Reg_A), .b(Reg_B), .out(subtractor_1_out));  // open: bin, bout
  Adder adder_2 (.a(Reg_A), .b(8'h1), .out(adder_2_out), .cout(Carry_Out));  // open: cin
  Subtractor subtractor_2 (.a(Reg_A), .b(8'h1), .out(subtractor_2_out));  // open: bin, bout
  assign not_1_out = ~Reg_A;  // NOT_Gate not_1, 8 bits wide
  AND8Bit and8bit_1 (.A(Reg_A), .B(Reg_B), .Res(and8bit_1_res));
  OR8Bit or8bit_1 (.A(Reg_A), .B(Reg_B), .Res(or8bit_1_res));
  XOR8Bit xor8bit_1 (.A(Reg_A), .B(Reg_B), .Res(xor8bit_1_res));
  assign ALU_Result = op_decoder_1_o0 ? adder_1_out : 8'bz;  // Controlled_Buffer controlled_buffer_1
  assign ALU_Result = op_decoder_1_o1 ? subtractor_1_out : 8'bz;  // Controlled_Buffer controlled_buffer_2
  assign ALU_Result = op_decoder_1_o2 ? adder_2_out : 8'bz;  // Controlled_Buffer controlled_buffer_3
  OP_Decoder op_decoder_1 (
    .OP(OP_ALU), .O0(op_decoder_1_o0), .O1(op_decoder_1_o1), .O2(op_decoder_1_o2), .O3(op_decoder_1_o3),
    .O4(op_decoder_1_o4), .O5(op_decoder_1_o5), .O6(op_decoder_1_o6), .O7(op_decoder_1_o7));
  assign ALU_Result = op_decoder_1_o3 ? subtractor_2_out : 8'bz;  // Controlled_Buffer controlled_buffer_4
  assign ALU_Result = op_decoder_1_o4 ? and8bit_1_res : 8'bz;  // Controlled_Buffer controlled_buffer_5
  assign ALU_Result = op_decoder_1_o5 ? or8bit_1_res : 8'bz;  // Controlled_Buffer controlled_buffer_6
  assign ALU_Result = op_decoder_1_o6 ? xor8bit_1_res : 8'bz;  // Controlled_Buffer controlled_buffer_7
  assign ALU_Result = op_decoder_1_o7 ? not_1_out : 8'bz;  // Controlled_Buffer controlled_buffer_8
  assign Dout = OE ? ALU_Result : 8'bz;  // Controlled_Buffer controlled_buffer_9
endmodule

module OP_Decoder (
  input  [2:0] OP,
  output O0,
  output O1,
  output O2,
  output O3,
  output O4,
  output O5,
  output O6,
  output O7
);

  wire not_1_out, not_2_out, not_3_out;

  not not_1 (not_1_out, OP[2]);
  not not_2 (not_2_out, OP[1]);
  not not_3 (not_3_out, OP[0]);
  and and_1 (O0, not_1_out, not_2_out, not_3_out);
  and and_2 (O1, not_1_out, not_2_out, OP[0]);
  and and_3 (O2, not_1_out, OP[1], not_3_out);
  and and_4 (O3, not_1_out, OP[1], OP[0]);
  and and_5 (O4, OP[2], not_2_out, not_3_out);
  and and_6 (O5, OP[2], not_2_out, OP[0]);
  and and_7 (O6, OP[2], OP[1], not_3_out);
  and and_8 (O7, OP[2], OP[1], OP[0]);
endmodule

module AND8Bit (
  input  [7:0] A,
  input  [7:0] B,
  output [7:0] Res
);

  and and_1 (Res[0], A[0], B[0]);
  and and_2 (Res[1], A[1], B[1]);
  and and_3 (Res[2], A[2], B[2]);
  and and_4 (Res[3], A[3], B[3]);
  and and_5 (Res[4], A[4], B[4]);
  and and_6 (Res[5], A[5], B[5]);
  and and_7 (Res[6], A[6], B[6]);
  and and_8 (Res[7], A[7], B[7]);
endmodule

module OR8Bit (
  input  [7:0] A,
  input  [7:0] B,
  output [7:0] Res
);

  or or_1 (Res[0], A[0], B[0]);
  or or_2 (Res[1], A[1], B[1]);
  or or_3 (Res[2], A[2], B[2]);
  or or_4 (Res[3], A[3], B[3]);
  or or_5 (Res[4], A[4], B[4]);
  or or_6 (Res[5], A[5], B[5]);
  or or_7 (Res[6], A[6], B[6]);
  or or_8 (Res[7], A[7], B[7]);
endmodule

module XOR8Bit (
  input  [7:0] A,
  input  [7:0] B,
  output [7:0] Res
);

  xor xor_1 (Res[0], A[0], B[0]);
  xor xor_2 (Res[1], A[1], B[1]);
  xor xor_3 (Res[2], A[2], B[2]);
  xor xor_4 (Res[3], A[3], B[3]);
  xor xor_5 (Res[4], A[4], B[4]);
  xor xor_6 (Res[5], A[5], B[5]);
  xor xor_7 (Res[6], A[6], B[6]);
  xor xor_8 (Res[7], A[7], B[7]);
endmodule
